// Logisim project tce.circ as structural Verilog
module main (
);

  wire cte_cu_1_p10, cte_cu_1_p11, cte_cu_1_p12, cte_cu_1_p13, dipswitch_1_sw1, dipswitch_1_sw2,
       dipswitch_1_sw3, dipswitch_1_sw4, dipswitch_1_sw5, dipswitch_1_sw6, dipswitch_1_sw7, dipswitch_1_sw8,
       dipswitch_2_sw4, dipswitch_2_sw5, dipswitch_2_sw6, dipswitch_2_sw7, dipswitch_2_sw8,
       mem_new_big_1_p16, mem_new_big_1_p18, mem_new_big_1_p20, mem_new_big_1_p22, mem_new_big_1_p32,
       mem_new_big_1_p33, mem_new_big_1_p34, mem_new_big_1_p35, mem_new_big_1_p36, mem_new_big_1_p37,
       mem_new_big_1_p38, mem_new_big_1_p39, mem_new_big_1_p40, register_1_q0, register_1_q1, register_1_q2,
       register_1_q3, register_1_q4, register_1_q5, register_1_q6, register_1_q7;

  DipSwitch dipswitch_1 (
    .sw1(dipswitch_1_sw1), .sw2(dipswitch_1_sw2), .sw3(dipswitch_1_sw3), .sw4(dipswitch_1_sw4),
    .sw5(dipswitch_1_sw5), .sw6(dipswitch_1_sw6), .sw7(dipswitch_1_sw7), .sw8(dipswitch_1_sw8));
  // mem_new_big mem_new_big_1: pin names not known; wires that end beside it: dipswitch_1_sw1, dipswitch_1_sw1, dipswitch_1_sw1, dipswitch_1_sw1, dipswitch_1_sw1, dipswitch_1_sw1, dipswitch_1_sw1, dipswitch_1_sw1, dipswitch_1_sw1, dipswitch_1_sw1, dipswitch_1_sw1, dipswitch_1_sw1, dipswitch_1_sw1, dipswitch_1_sw1, dipswitch_1_sw1, mem_new_big_1_p16, mem_new_big_1_p16, mem_new_big_1_p18, mem_new_big_1_p18, mem_new_big_1_p20, mem_new_big_1_p20, mem_new_big_1_p22, mem_new_big_1_p22, dipswitch_1_sw8, dipswitch_1_sw7, dipswitch_1_sw6, dipswitch_1_sw5, dipswitch_1_sw4, dipswitch_1_sw3, dipswitch_1_sw2, dipswitch_1_sw1, mem_new_big_1_p32, mem_new_big_1_p33, mem_new_big_1_p34, mem_new_big_1_p35, mem_new_big_1_p36, mem_new_big_1_p37, mem_new_big_1_p38, mem_new_big_1_p39, mem_new_big_1_p40
  DipSwitch dipswitch_2 (
    .sw1(mem_new_big_1_p38), .sw2(mem_new_big_1_p39), .sw3(mem_new_big_1_p40), .sw4(dipswitch_2_sw4),
    .sw5(dipswitch_2_sw5), .sw6(dipswitch_2_sw6), .sw7(dipswitch_2_sw7), .sw8(dipswitch_2_sw8));
  register register_1 (
    .Q0(register_1_q0), .Q1(register_1_q1), .Q2(register_1_q2), .Q3(register_1_q3), .Q4(register_1_q4),
    .Q5(register_1_q5), .Q6(register_1_q6), .Q7(register_1_q7), .en_input(cte_cu_1_p12),
    .clock(mem_new_big_1_p32), .D0(mem_new_big_1_p33), .D1(mem_new_big_1_p34), .D2(mem_new_big_1_p35),
    .D3(mem_new_big_1_p36), .D4(mem_new_big_1_p37), .en_output(1'b1));  // open: out_12, out_13, out_14, out_15, out_16, out_17, out_18, DG0, D5, D6, D7
  Clock clock_1 (.out(mem_new_big_1_p32));
  // cte_cu cte_cu_1: pin names not known; wires that end beside it: register_1_q0, register_1_q1, register_1_q2, register_1_q3, register_1_q4, register_1_q5, register_1_q6, register_1_q7, mem_new_big_1_p32, cte_cu_1_p10, cte_cu_1_p11, cte_cu_1_p12, cte_cu_1_p13
endmodule

// tce
module tce_alu (
  input  in_1,
  input  in_2,
  input  in_3,
  input  in_4,
  input  in_5,
  input  in_6,
  input  in_7,
  input  in_8,
  input  A8,
  input  in_10,
  input  in_11,
  input  in_12,
  input  in_13,
  input  in_14,
  input  in_15,
  input  A1,
  input  alu_out,
  input  clock,
  input  Cin,
  input  CTRL0,
  input  CTRL1,
  input  CTRL2,
  output O0,
  output O1,
  output O2,
  output O3,
  output O4,
  output O5,
  output O6,
  output O7,
  output Cout
);

  wire alu_calc_1_p18, alu_calc_1_p19, alu_calc_1_p20, alu_calc_1_p21, alu_calc_1_p22, alu_calc_1_p23,
       alu_calc_1_p24, alu_calc_1_p25, alu_calc_1_p26, alu_calc_1_p27, alu_decoder_1_and,
       alu_decoder_1_o_not, alu_decoder_1_or, alu_decoder_1_xor, and_1_out;

  // alu_calc alu_calc_1: pin names not known; wires that end beside it: A1, in_15, in_14, in_13, in_12, in_11, in_10, A8, Cin, in_8, in_7, in_6, in_5, in_4, in_3, in_2, in_1, alu_calc_1_p18, alu_calc_1_p19, alu_calc_1_p20, alu_calc_1_p21, alu_calc_1_p22, alu_calc_1_p23, alu_calc_1_p24, alu_calc_1_p25, alu_calc_1_p26, alu_calc_1_p27, alu_calc_1_p21
  alu_and alu_and_1 (
    .N0(alu_calc_1_p18), .N1(alu_calc_1_p19), .N2(alu_calc_1_p20), .N3(alu_calc_1_p21), .N4(alu_calc_1_p22),
    .N5(alu_calc_1_p23), .N6(alu_calc_1_p24), .N7(alu_calc_1_p25), .X3(in_13), .X2(in_14), .X1(in_15),
    .X0(A1), .Y7(in_1), .Y6(in_2), .Y5(in_3), .Y4(in_4), .X7(A8), .Y3(in_5), .Y2(in_6), .Y1(in_7), .Y0(in_8),
    .X6(in_10), .X5(in_11), .X4(in_12), .en(alu_decoder_1_and));
  alu_or alu_or_1 (
    .N0(alu_calc_1_p18), .N1(alu_calc_1_p19), .N2(alu_calc_1_p20), .N3(alu_calc_1_p21), .N4(alu_calc_1_p22),
    .N5(alu_calc_1_p23), .N6(alu_calc_1_p24), .N7(alu_calc_1_p25), .B0(in_8), .B1(in_7), .in_11(in_6),
    .in_12(in_5), .in_13(in_4), .in_14(in_3), .in_15(in_2), .B7(in_1), .en(alu_decoder_1_or), .A7(A8),
    .A6(in_10), .in_3(in_11), .in_4(in_12), .in_5(in_13), .in_6(in_14), .in_7(in_15), .A0(A1));
  alu_xor alu_xor_1 (
    .out_18(alu_calc_1_p18), .out_19(alu_calc_1_p19), .out_20(alu_calc_1_p20), .out_21(alu_calc_1_p21),
    .out_22(alu_calc_1_p22), .out_23(alu_calc_1_p23), .out_24(alu_calc_1_p24), .out_25(alu_calc_1_p25),
    .B0(in_8), .B1(in_7), .in_11(in_6), .in_12(in_5), .in_13(in_4), .in_14(in_3), .in_15(in_2), .B7(in_1),
    .en(alu_decoder_1_xor), .A7(A8), .A6(in_10), .in_3(in_11), .in_4(in_12), .in_5(in_13), .in_6(in_14),
    .in_7(in_15), .A0(A1));
  bus_transceiver bus_transceiver_1 (
    .in_2(alu_calc_1_p25), .in_3(alu_calc_1_p24), .in_4(alu_calc_1_p23), .in_5(alu_calc_1_p22),
    .in_6(alu_calc_1_p21), .in_7(alu_calc_1_p20), .in_8(alu_calc_1_p19), .enable(alu_calc_1_p18),
    .out_11(alu_calc_1_p25), .out_12(alu_calc_1_p24), .out_13(alu_calc_1_p23), .out_14(alu_calc_1_p22),
    .out_15(alu_calc_1_p21), .out_16(alu_calc_1_p20), .out_17(alu_calc_1_p19));  // open: in_1, out_10
  and and_1 (and_1_out, alu_out, clock);
  alu_decoder alu_decoder_1 (
    .ADD(alu_calc_1_p26), .SUb(alu_calc_1_p27), .AND(alu_decoder_1_and), .OR(alu_decoder_1_or),
    .XOR(alu_decoder_1_xor), .O_NOT(alu_decoder_1_o_not), .CTRL0(CTRL0), .CTRL1(CTRL1), .CTRL2(CTRL2));
endmodule

module alu_decoder (
  input  CTRL0,
  input  CTRL1,
  input  CTRL2,
  output ADD,
  output SUb,
  output AND,
  output OR,
  output XOR,
  output O_NOT
);

  wire NotCtrl0, NotCtrl1, NotCtrl2;

  _7404 u_7404_1 (
    .pin13(CTRL2), .pin12(NotCtrl2), .pin11(CTRL1), .pin10(NotCtrl1), .pin9(CTRL0), .pin8(NotCtrl0));  // open: pin1, pin2, pin3, pin4, pin5, pin6
  _7411 u_7411_1 (
    .pin1(NotCtrl1), .pin2(NotCtrl2), .pin3(NotCtrl0), .pin4(CTRL1), .pin5(NotCtrl2), .pin6(AND),
    .pin13(CTRL0), .pin12(SUb), .pin11(NotCtrl2), .pin10(NotCtrl1), .pin9(NotCtrl0), .pin8(ADD));
  _7411 u_7411_2 (
    .pin1(NotCtrl1), .pin2(CTRL2), .pin3(CTRL0), .pin4(NotCtrl1), .pin5(CTRL2), .pin6(O_NOT),
    .pin13(NotCtrl0), .pin12(XOR), .pin11(NotCtrl2), .pin10(CTRL1), .pin9(CTRL0), .pin8(OR));

  // Other names for the same wires on the sheet: S_NOT = O_NOT
endmodule

module alu_output_controller (
  input  E0,
  input  E,
  input  in_3,
  input  in_4,
  input  in_5,
  input  in_6,
  input  in_7,
  input  E7,
  input  N0,
  input  in_10,
  input  in_11,
  input  in_12,
  input  in_13,
  input  in_14,
  input  N,
  input  N7,
  input  V0,
  input  in_18,
  input  in_19,
  input  in_20,
  input  in_21,
  input  in_22,
  input  V,
  input  V7,
  input  X0,
  input  in_26,
  input  in_27,
  input  in_28,
  input  in_29,
  input  X,
  input  in_31,
  input  X7,
  input  clock,
  input  alu_out,
  output O0,
  output O1,
  output O2,
  output O3,
  output O4,
  output O5,
  output O6,
  output O7
);

  wire n7432_1_pin1, n7432_1_pin2, n7432_1_pin3, n7432_2_pin1, n7432_2_pin2, n7432_2_pin3, n7432_3_pin1,
       n7432_3_pin2, n7432_3_pin3, n7432_4_pin1, n7432_4_pin2, n7432_4_pin3, n7432_5_pin1, n7432_5_pin2,
       n7432_5_pin3, n7432_6_pin1, n7432_6_pin2, n7432_6_pin3, n7432_7_pin1, n7432_7_pin2, n7432_7_pin3,
       n7432_8_pin1, n7432_8_pin2, n7432_8_pin3;

  _7432 u_7432_1 (
    .pin1(n7432_1_pin1), .pin2(n7432_1_pin2), .pin3(n7432_1_pin3), .pin13(X0), .pin12(V0),
    .pin11(n7432_1_pin1), .pin10(N0), .pin9(E0), .pin8(n7432_1_pin2));  // open: pin4, pin5, pin6
  _7432 u_7432_2 (
    .pin1(n7432_2_pin1), .pin2(n7432_2_pin2), .pin3(n7432_2_pin3), .pin13(in_26), .pin12(in_18),
    .pin11(n7432_2_pin1), .pin10(in_10), .pin9(E), .pin8(n7432_2_pin2));  // open: pin4, pin5, pin6
  _7432 u_7432_3 (
    .pin1(n7432_3_pin1), .pin2(n7432_3_pin2), .pin3(n7432_3_pin3), .pin13(in_27), .pin12(in_19),
    .pin11(n7432_3_pin1), .pin10(in_11), .pin9(in_3), .pin8(n7432_3_pin2));  // open: pin4, pin5, pin6
  _7432 u_7432_4 (
    .pin1(n7432_4_pin1), .pin2(n7432_4_pin2), .pin3(n7432_4_pin3), .pin13(in_28), .pin12(in_20),
    .pin11(n7432_4_pin1), .pin10(in_12), .pin9(in_4), .pin8(n7432_4_pin2));  // open: pin4, pin5, pin6
  _7432 u_7432_5 (
    .pin1(n7432_5_pin1), .pin2(n7432_5_pin2), .pin3(n7432_5_pin3), .pin13(in_29), .pin12(in_21),
    .pin11(n7432_5_pin1), .pin10(in_13), .pin9(in_5), .pin8(n7432_5_pin2));  // open: pin4, pin5, pin6
  _7432 u_7432_6 (
    .pin1(n7432_6_pin1), .pin2(n7432_6_pin2), .pin3(n7432_6_pin3), .pin13(X), .pin12(in_22),
    .pin11(n7432_6_pin1), .pin10(in_14), .pin9(in_6), .pin8(n7432_6_pin2));  // open: pin4, pin5, pin6
  _7411 u_7411_1 (
    .pin1(n7432_1_pin3), .pin2(alu_out), .pin3(alu_out), .pin4(clock), .pin5(n7432_2_pin3), .pin6(O1),
    .pin13(clock), .pin12(O0), .pin11(clock), .pin10(n7432_3_pin3), .pin9(alu_out), .pin8(O2));
  _7411 u_7411_2 (
    .pin1(n7432_4_pin3), .pin2(alu_out), .pin3(alu_out), .pin4(clock), .pin5(n7432_5_pin3), .pin6(O4),
    .pin13(clock), .pin12(O3), .pin11(clock), .pin10(n7432_6_pin3), .pin9(alu_out), .pin8(O5));
  _7432 u_7432_7 (
    .pin1(n7432_7_pin1), .pin2(n7432_7_pin2), .pin3(n7432_7_pin3), .pin13(in_31), .pin12(V),
    .pin11(n7432_7_pin1), .pin10(N), .pin9(in_7), .pin8(n7432_7_pin2));  // open: pin4, pin5, pin6
  _7432 u_7432_8 (
    .pin1(n7432_8_pin1), .pin2(n7432_8_pin2), .pin3(n7432_8_pin3), .pin13(X7), .pin12(V7),
    .pin11(n7432_8_pin1), .pin10(N7), .pin9(E7), .pin8(n7432_8_pin2));  // open: pin4, pin5, pin6
  _7411 u_7411_3 (
    .pin1(n7432_7_pin3), .pin2(alu_out), .pin3(alu_out), .pin4(clock), .pin5(n7432_8_pin3), .pin6(O7),
    .pin13(clock), .pin12(O6), .pin11(clock), .pin9(alu_out));  // open: pin10, pin8

  // Other names for the same wires on the sheet: E1 = E; E2 = in_3; E3 = in_4; E4 = in_5; E5 = in_6; E6 = in_7;
  //   N1 = in_10; N2 = in_11; N3 = in_12; N4 = in_13; N5 = in_14; N6 = N; V1 = in_18; V2 = in_19; V3 = in_20;
  //   V4 = in_21; V5 = in_22; V6 = V; X1 = in_26; X2 = in_27; X3 = in_28; X4 = in_29; X5 = X; X6 = in_31

  // Notes on the sheet:
  //   OUTPUT CONTROLLER
endmodule

module alu_and (
  input  X7,
  input  X6,
  input  X5,
  input  X4,
  input  X3,
  input  X2,
  input  X1,
  input  X0,
  input  Y7,
  input  Y6,
  input  Y5,
  input  Y4,
  input  Y3,
  input  Y2,
  input  Y1,
  input  Y0,
  input  en,
  output N0,
  output N1,
  output N2,
  output N3,
  output N4,
  output N5,
  output N6,
  output N7
);

  wire n7408_1_pin3, n7408_1_pin6, n7408_1_pin8, n7408_1_pin11, n7408_2_pin3, n7408_2_pin6, n7408_2_pin8,
       n7408_2_pin11;

  _7408 u_7408_1 (
    .pin1(X2), .pin2(Y2), .pin3(n7408_1_pin3), .pin4(X3), .pin5(Y3), .pin6(n7408_1_pin6), .pin13(Y1),
    .pin12(X1), .pin11(n7408_1_pin11), .pin10(Y0), .pin9(X0), .pin8(n7408_1_pin8));
  _7408 u_7408_2 (
    .pin1(X6), .pin2(Y6), .pin3(n7408_2_pin3), .pin4(X7), .pin5(Y7), .pin6(n7408_2_pin6), .pin13(Y5),
    .pin12(X5), .pin11(n7408_2_pin11), .pin10(Y4), .pin9(X4), .pin8(n7408_2_pin8));
  bus_transceiver bus_transceiver_1 (
    .in_1(n7408_1_pin8), .in_2(n7408_1_pin11), .in_3(n7408_1_pin3), .in_4(n7408_1_pin6), .in_5(n7408_2_pin8),
    .in_6(n7408_2_pin11), .in_7(n7408_2_pin3), .in_8(n7408_2_pin6), .enable(en), .out_10(N0), .out_11(N1),
    .out_12(N2), .out_13(N3), .out_14(N4), .out_15(N5), .out_16(N6), .out_17(N7));

  // Notes on the sheet:
  //   X0: pull=up
  //   Y0: pull=up
endmodule

module alu_or (
  input  A7,
  input  A6,
  input  in_3,
  input  in_4,
  input  in_5,
  input  in_6,
  input  in_7,
  input  A0,
  input  B0,
  input  B1,
  input  in_11,
  input  in_12,
  input  in_13,
  input  in_14,
  input  in_15,
  input  B7,
  input  en,
  output N0,
  output N1,
  output N2,
  output N3,
  output N4,
  output N5,
  output N6,
  output N7
);

  wire n7432_1_pin3, n7432_1_pin6, n7432_1_pin8, n7432_2_pin3, n7432_2_pin6, n7432_2_pin8, n7432_2_pin11;

  _7432 u_7432_1 (
    .pin1(in_5), .pin2(in_12), .pin3(n7432_1_pin3), .pin4(in_6), .pin5(in_11), .pin6(n7432_1_pin6),
    .pin13(B1), .pin12(in_7), .pin11(A0), .pin10(B0), .pin9(A0), .pin8(n7432_1_pin8));
  _7432 u_7432_2 (
    .pin1(A7), .pin2(B7), .pin3(n7432_2_pin3), .pin4(A6), .pin5(in_15), .pin6(n7432_2_pin6), .pin13(in_14),
    .pin12(in_3), .pin11(n7432_2_pin11), .pin10(in_13), .pin9(in_4), .pin8(n7432_2_pin8));
  bus_transceiver bus_transceiver_1 (
    .in_2(n7432_1_pin8), .in_3(A0), .in_4(n7432_1_pin6), .in_5(n7432_1_pin3), .in_6(n7432_2_pin8),
    .in_7(n7432_2_pin11), .in_8(n7432_2_pin6), .enable(n7432_2_pin3), .out_11(n7432_1_pin8), .out_12(A0),
    .out_13(n7432_1_pin6), .out_14(n7432_1_pin3), .out_15(n7432_2_pin8), .out_16(n7432_2_pin11),
    .out_17(n7432_2_pin6));  // open: in_1, out_10

  // Other names for the same wires on the sheet: A1 = in_7; A2 = in_6; A3 = in_5; A4 = in_4; A5 = in_3; B2 = in_11;
  //   B3 = in_12; B4 = in_13; B5 = in_14; B6 = in_15

  // Notes on the sheet:
  //   B0: pull=up
  //   B1: pull=up
  //   A0: pull=up
  //   AND
endmodule

module alu_xor (
  input  A7,
  input  A6,
  input  in_3,
  input  in_4,
  input  in_5,
  input  in_6,
  input  in_7,
  input  A0,
  input  B0,
  input  B1,
  input  in_11,
  input  in_12,
  input  in_13,
  input  in_14,
  input  in_15,
  input  B7,
  input  en,
  output out_18,
  output out_19,
  output out_20,
  output out_21,
  output out_22,
  output out_23,
  output out_24,
  output out_25
);

  wire n7486_1_pin3, n7486_1_pin6, n7486_1_pin8, n7486_1_pin11, n7486_2_pin6, n7486_2_pin8, n7486_2_pin11;

  _7486 u_7486_1 (
    .pin1(in_5), .pin2(in_12), .pin3(n7486_1_pin3), .pin4(in_6), .pin5(in_11), .pin6(n7486_1_pin6),
    .pin13(B1), .pin12(in_7), .pin11(n7486_1_pin11), .pin10(B0), .pin9(A0), .pin8(n7486_1_pin8));
  _7486 u_7486_2 (
    .pin1(A7), .pin2(B7), .pin3(en), .pin4(A6), .pin5(in_15), .pin6(n7486_2_pin6), .pin13(in_14),
    .pin12(in_3), .pin11(n7486_2_pin11), .pin10(in_13), .pin9(in_4), .pin8(n7486_2_pin8));
  bus_transceiver bus_transceiver_1 (
    .in_2(n7486_1_pin8), .in_3(n7486_1_pin11), .in_4(n7486_1_pin6), .in_5(n7486_1_pin3), .in_6(n7486_2_pin8),
    .in_7(n7486_2_pin11), .in_8(n7486_2_pin6), .enable(en), .out_11(n7486_1_pin8), .out_12(n7486_1_pin11),
    .out_13(n7486_1_pin6), .out_14(n7486_1_pin3), .out_15(n7486_2_pin8), .out_16(n7486_2_pin11),
    .out_17(n7486_2_pin6));  // open: in_1, out_10

  // Other names for the same wires on the sheet: A1 = in_7; A2 = in_6; A3 = in_5; A4 = in_4; A5 = in_3; B2 = in_11;
  //   B3 = in_12; B4 = in_13; B5 = in_14; B6 = in_15; XOR = en

  // Notes on the sheet:
  //   B0: pull=up
  //   B1: pull=up
  //   A0: pull=up
  //   AND
endmodule

module alu_calc (
  input  A7,
  input  A6,
  input  in_3,
  input  in_4,
  input  in_5,
  input  in_6,
  input  in_7,
  input  A0,
  input  B7,
  input  in_10,
  input  in_11,
  input  in_12,
  input  in_13,
  input  in_14,
  input  B1,
  input  B0,
  input  Cin,
  input  ADD,
  input  SUB,
  output N0,
  output N1,
  output N2,
  output N3,
  output N4,
  output N5,
  output N6,
  output N7,
  output CARRY
);

  wire B_OR_SUB0, B_OR_SUB1, B_OR_SUB2, B_OR_SUB3, B_OR_SUB4, B_OR_SUB5, B_OR_SUB6, B_OR_SUB7, CALC,
       Cin_OR_SUB, n7408_1_pin3, n7408_1_pin6, n7408_1_pin8, n7408_1_pin11, n7408_2_pin3, n7408_2_pin6,
       n7408_2_pin8, n7408_2_pin11, n7408_3_pin3, n7408_3_pin6, n7408_3_pin8, n7408_3_pin11, n7408_4_pin3,
       n7408_4_pin6, n7408_4_pin8, n7408_4_pin11, n7432_4_pin11, n7486_3_pin1, n7486_3_pin2, n7486_3_pin3,
       n7486_3_pin5, n7486_3_pin6, n7486_4_pin1, n7486_4_pin2, n7486_4_pin3, n7486_4_pin4, n7486_4_pin5,
       n7486_4_pin6, n7486_5_pin1, n7486_5_pin2, n7486_5_pin3, n7486_5_pin4, n7486_5_pin5, n7486_5_pin6,
       n7486_6_pin1, n7486_6_pin2, n7486_6_pin3, n7486_6_pin4, n7486_6_pin5, n7486_6_pin6, xor_2_out;

  or or_1 (CALC, ADD, SUB);
  xor xor_1 (Cin_OR_SUB, SUB, Cin);
  _7486 u_7486_1 (
    .pin1(SUB), .pin2(in_13), .pin3(B_OR_SUB3), .pin4(SUB), .pin5(in_14), .pin6(B_OR_SUB2), .pin13(SUB),
    .pin12(B1), .pin11(B_OR_SUB1), .pin10(SUB), .pin9(B0), .pin8(B_OR_SUB0));
  _7486 u_7486_2 (
    .pin1(SUB), .pin2(B7), .pin3(B_OR_SUB7), .pin4(SUB), .pin5(in_10), .pin6(B_OR_SUB6), .pin13(SUB),
    .pin12(in_11), .pin11(B_OR_SUB5), .pin10(SUB), .pin9(in_12), .pin8(B_OR_SUB4));
  _7486 u_7486_3 (
    .pin1(n7486_3_pin1), .pin2(n7486_3_pin2), .pin3(n7486_3_pin3), .pin4(Cin_OR_SUB), .pin5(n7486_3_pin5),
    .pin6(n7486_3_pin6), .pin13(B_OR_SUB1), .pin12(in_7), .pin11(n7486_3_pin1), .pin10(B_OR_SUB0), .pin9(A0),
    .pin8(n7486_3_pin5));
  _7486 u_7486_4 (
    .pin1(n7486_4_pin1), .pin2(n7486_4_pin2), .pin3(n7486_4_pin3), .pin4(n7486_4_pin4), .pin5(n7486_4_pin5),
    .pin6(n7486_4_pin6), .pin13(B_OR_SUB3), .pin12(in_5), .pin11(n7486_4_pin1), .pin10(B_OR_SUB2),
    .pin9(in_6), .pin8(n7486_4_pin5));
  _7486 u_7486_5 (
    .pin1(n7486_5_pin1), .pin2(n7486_5_pin2), .pin3(n7486_5_pin3), .pin4(n7486_5_pin4), .pin5(n7486_5_pin5),
    .pin6(n7486_5_pin6), .pin13(B_OR_SUB5), .pin12(in_3), .pin11(n7486_5_pin1), .pin10(B_OR_SUB4),
    .pin9(in_4), .pin8(n7486_5_pin5));
  _7486 u_7486_6 (
    .pin1(n7486_6_pin1), .pin2(n7486_6_pin2), .pin3(n7486_6_pin3), .pin4(n7486_6_pin4), .pin5(n7486_6_pin5),
    .pin6(n7486_6_pin6), .pin13(B_OR_SUB7), .pin12(A7), .pin11(n7486_6_pin1), .pin10(B_OR_SUB6), .pin9(A6),
    .pin8(n7486_6_pin5));
  _7408 u_7408_1 (
    .pin1(n7486_3_pin1), .pin2(n7486_3_pin2), .pin3(n7408_1_pin3), .pin4(n7486_3_pin5), .pin5(Cin_OR_SUB),
    .pin6(n7408_1_pin6), .pin13(in_7), .pin12(B_OR_SUB1), .pin11(n7408_1_pin11), .pin10(A0),
    .pin9(B_OR_SUB0), .pin8(n7408_1_pin8));
  _7408 u_7408_2 (
    .pin1(n7486_4_pin1), .pin2(n7486_4_pin2), .pin3(n7408_2_pin3), .pin4(n7486_4_pin5), .pin5(n7486_4_pin4),
    .pin6(n7408_2_pin6), .pin13(in_5), .pin12(B_OR_SUB3), .pin11(n7408_2_pin11), .pin10(in_6),
    .pin9(B_OR_SUB2), .pin8(n7408_2_pin8));
  _7408 u_7408_3 (
    .pin1(n7486_5_pin1), .pin2(n7486_5_pin2), .pin3(n7408_3_pin3), .pin4(n7486_5_pin5), .pin5(n7486_5_pin4),
    .pin6(n7408_3_pin6), .pin13(in_3), .pin12(B_OR_SUB5), .pin11(n7408_3_pin11), .pin10(in_4),
    .pin9(B_OR_SUB4), .pin8(n7408_3_pin8));
  _7408 u_7408_4 (
    .pin1(n7486_6_pin1), .pin2(n7486_6_pin2), .pin3(n7408_4_pin3), .pin4(n7486_6_pin5), .pin5(n7486_6_pin4),
    .pin6(n7408_4_pin6), .pin13(A7), .pin12(B_OR_SUB7), .pin11(n7408_4_pin11), .pin10(A6), .pin9(B_OR_SUB6),
    .pin8(n7408_4_pin8));
  _7432 u_7432_1 (
    .pin13(n7408_1_pin11), .pin12(n7408_1_pin3), .pin11(n7486_4_pin4), .pin10(n7408_1_pin6),
    .pin9(n7408_1_pin8), .pin8(n7486_3_pin2));  // open: pin1, pin2, pin3, pin4, pin5, pin6
  _7432 u_7432_2 (
    .pin13(n7408_2_pin11), .pin12(n7408_2_pin3), .pin11(n7486_5_pin4), .pin10(n7408_2_pin6),
    .pin9(n7408_2_pin8), .pin8(n7486_4_pin2));  // open: pin1, pin2, pin3, pin4, pin5, pin6
  _7432 u_7432_3 (
    .pin13(n7408_3_pin11), .pin12(n7408_3_pin3), .pin11(n7486_6_pin4), .pin10(n7408_3_pin6),
    .pin9(n7408_3_pin8), .pin8(n7486_5_pin2));  // open: pin1, pin2, pin3, pin4, pin5, pin6
  _7432 u_7432_4 (
    .pin13(n7408_4_pin11), .pin12(n7408_4_pin3), .pin11(n7432_4_pin11), .pin10(n7408_4_pin6),
    .pin9(n7408_4_pin8), .pin8(n7486_6_pin2));  // open: pin1, pin2, pin3, pin4, pin5, pin6
  xor xor_2 (xor_2_out, n7432_4_pin11, SUB);
  bus_transceiver bus_transceiver_1 (
    .in_1(n7486_3_pin6), .in_2(n7486_3_pin3), .in_3(n7486_4_pin6), .in_4(n7486_4_pin3), .in_5(n7486_5_pin6),
    .in_6(n7486_5_pin3), .in_7(n7486_6_pin6), .in_8(n7486_6_pin3), .enable(CALC), .out_10(N0), .out_11(N1),
    .out_12(N2), .out_13(N3), .out_14(N4), .out_15(N5), .out_16(N6), .out_17(N7));
  and and_1 (CARRY, xor_2_out, CALC);

  // Other names for the same wires on the sheet: A1 = in_7; A2 = in_6; A3 = in_5; A4 = in_4; A5 = in_3; B2 = in_14;
  //   B3 = in_13; B4 = in_12; B5 = in_11; B6 = in_10

  // Notes on the sheet:
  //   A0: pull=up
  //   B1: pull=up
  //   B0: pull=up
endmodule

module register (
  input  D0,
  input  D1,
  input  D2,
  input  D3,
  input  D4,
  input  D5,
  input  D6,
  input  D7,
  input  en_input,
  input  clock,
  input  en_output,
  output out_12,
  output out_13,
  output out_14,
  output out_15,
  output out_16,
  output out_17,
  output out_18,
  output DG0,
  output Q0,
  output Q1,
  output Q2,
  output Q3,
  output Q4,
  output Q5,
  output Q6,
  output Q7
);

  Register #(.width(1)) register_1 (.D(D0), .en(en_input), .clk(clock), .Q(DG0));  // open: clr
  Register #(.width(1)) register_2 (.D(D1), .en(en_input), .clk(clock), .Q(out_18));  // open: clr
  Register #(.width(1)) register_3 (.D(D2), .en(en_input), .clk(clock), .Q(out_17));  // open: clr
  Register #(.width(1)) register_4 (.D(D3), .en(en_input), .clk(clock), .Q(out_16));  // open: clr
  Register #(.width(1)) register_5 (.D(D4), .en(en_input), .clk(clock), .Q(out_15));  // open: clr
  Register #(.width(1)) register_6 (.D(D5), .en(en_input), .clk(clock), .Q(out_14));  // open: clr
  Register #(.width(1)) register_7 (.D(D6), .en(en_input), .clk(clock), .Q(out_13));  // open: clr
  Register #(.width(1)) register_8 (.D(D7), .en(en_input), .clk(clock), .Q(out_12));  // open: clr
  assign Q0 = en_output ? DG0 : 1'bz;  // Controlled_Buffer controlled_buffer_1
  assign Q1 = en_output ? out_18 : 1'bz;  // Controlled_Buffer controlled_buffer_2
  assign Q2 = en_output ? out_17 : 1'bz;  // Controlled_Buffer controlled_buffer_3
  assign Q3 = en_output ? out_16 : 1'bz;  // Controlled_Buffer controlled_buffer_4
  assign Q4 = en_output ? out_15 : 1'bz;  // Controlled_Buffer controlled_buffer_5
  assign Q5 = en_output ? out_14 : 1'bz;  // Controlled_Buffer controlled_buffer_6
  assign Q6 = en_output ? out_13 : 1'bz;  // Controlled_Buffer controlled_buffer_7
  assign Q7 = en_output ? out_12 : 1'bz;  // Controlled_Buffer controlled_buffer_8
endmodule

module memory (
  input  A7,
  input  in_2,
  input  in_3,
  input  in_4,
  input  in_5,
  input  in_6,
  input  in_7,
  input  A0,
  input  D0,
  input  in_10,
  input  in_11,
  input  in_12,
  input  in_13,
  input  in_14,
  input  in_15,
  input  D7,
  input  clock,
  input  en_read,
  input  en_write,
  output Q0,
  output out_21,
  output out_22,
  output out_23,
  output out_24,
  output out_25,
  output out_26,
  output Q7
);

  wire [7:0] ram_1_dout;

  RAM ram_1 (
    .addr({A7, in_2, in_3, in_4, in_5, in_6, in_7, A0}), .we(en_write), .oe(en_read), .clk(clock),
    .din({D7, in_15, in_14, in_13, in_12, in_11, in_10, D0}), .dout(ram_1_dout));
  assign {Q7, out_26, out_25, out_24, out_23, out_22, out_21, Q0} = en_read ? ram_1_dout : 8'bz;  // Controlled_Buffer controlled_buffer_1
endmodule

module pc (
  input  [7:0] A,
  input  enabled,
  input  reset,
  input  jump,
  input  count,
  input  clock,
  output out_7,
  output out_8,
  output out_9,
  output out_10,
  output out_11,
  output out_12,
  output out_13,
  output out_14,
  output [7:0] O
);

  Counter counter_1 (
    .clr(reset), .load(jump), .up(1'b1), .count(count), .clk(clock), .D(A),
    .Q({out_7, out_8, out_9, out_10, out_11, out_12, out_13, out_14}));  // open: carry
  assign O = enabled ? {out_7, out_8, out_9, out_10, out_11, out_12, out_13, out_14} : 8'bz;  // Controlled_Buffer controlled_buffer_1
endmodule

module hexdisplaydecoder (
  input  in_1,
  input  in_2,
  input  in_3,
  input  in_4
);

  wire decoder_1_out_5, decoder_1_out_6, decoder_1_out_7, decoder_1_out_8, decoder_1_out_9, decoder_1_out_10,
       decoder_1_out_11, decoder_1_out_12, decoder_1_out_13, decoder_1_out_14, decoder_1_out_15,
       decoder_1_out_16, decoder_1_out_17, decoder_1_out_18, decoder_1_out_19, decoder_1_out_20, not_1_out,
       not_2_out, not_3_out, not_4_out, not_5_out, not_6_out, not_7_out, or_1_out, or_2_out, or_3_out,
       or_4_out, or_5_out, or_6_out, or_7_out, or_8_out, or_9_out, or_10_out, or_11_out, or_12_out;

  decoder decoder_1 (
    .D0(in_1), .in_2(in_2), .in_3(in_3), .in_4(in_4), .out_5(decoder_1_out_5), .out_6(decoder_1_out_6),
    .out_7(decoder_1_out_7), .out_8(decoder_1_out_8), .out_9(decoder_1_out_9), .out_10(decoder_1_out_10),
    .out_11(decoder_1_out_11), .out_12(decoder_1_out_12), .out_13(decoder_1_out_13),
    .out_14(decoder_1_out_14), .out_15(decoder_1_out_15), .out_16(decoder_1_out_16),
    .out_17(decoder_1_out_17), .out_18(decoder_1_out_18), .out_19(decoder_1_out_19), .out_20(decoder_1_out_20));
  or or_1 (or_1_out, decoder_1_out_19, decoder_1_out_10, decoder_1_out_8, decoder_1_out_7);
  or or_2 (or_2_out, decoder_1_out_15, decoder_1_out_14, decoder_1_out_10, decoder_1_out_9);
  or or_3 (or_3_out, decoder_1_out_18, decoder_1_out_16, decoder_1_out_9, decoder_1_out_5);
  or or_4 (or_4_out, decoder_1_out_19, decoder_1_out_16, decoder_1_out_13, decoder_1_out_12);
  or or_5 (or_5_out, decoder_1_out_19, decoder_1_out_17, decoder_1_out_16, decoder_1_out_15);
  or or_6 (or_6_out, decoder_1_out_19, decoder_1_out_18, decoder_1_out_13, decoder_1_out_7);
  or or_7 (or_7_out, decoder_1_out_19, decoder_1_out_17, decoder_1_out_13, decoder_1_out_20);
  not not_1 (not_1_out, or_1_out);
  or or_8 (or_8_out, decoder_1_out_5, decoder_1_out_6, or_2_out);
  or or_9 (or_9_out, decoder_1_out_6, or_3_out);
  or or_10 (or_10_out, decoder_1_out_11, decoder_1_out_5, or_4_out);
  or or_11 (or_11_out, decoder_1_out_13, decoder_1_out_12, or_5_out);
  not not_2 (not_2_out, or_6_out);
  or or_12 (or_12_out, decoder_1_out_9, or_7_out);
  not not_3 (not_3_out, or_12_out);
  not not_4 (not_4_out, or_8_out);
  not not_5 (not_5_out, or_9_out);
  not not_6 (not_6_out, or_10_out);
  not not_7 (not_7_out, or_11_out);
  _7_Segment_Display u_7_segment_display_1 (
    .g(not_3_out), .f(not_2_out), .a(not_1_out), .b(not_4_out), .e(not_7_out), .d(not_6_out), .c(not_5_out));  // open: dp
endmodule

module decoder (
  input  D0,
  input  in_2,
  input  in_3,
  input  in_4,
  output out_5,
  output out_6,
  output out_7,
  output out_8,
  output out_9,
  output out_10,
  output out_11,
  output out_12,
  output out_13,
  output out_14,
  output out_15,
  output out_16,
  output out_17,
  output out_18,
  output out_19,
  output out_20
);

  wire not_1_out, not_2_out, not_3_out, not_4_out;

  not not_1 (not_1_out, D0);
  not not_2 (not_2_out, in_2);
  not not_3 (not_3_out, in_3);
  not not_4 (not_4_out, in_4);
  and and_1 (out_20, not_1_out, not_2_out, not_3_out, not_4_out);
  and and_2 (out_19, D0, not_2_out, not_3_out, not_4_out);
  and and_3 (out_18, not_1_out, in_2, not_3_out, not_4_out);
  and and_4 (out_17, D0, in_2, not_3_out, not_4_out);
  and and_5 (out_16, not_1_out, not_2_out, in_3, not_4_out);
  and and_6 (out_15, D0, not_2_out, in_3, not_4_out);
  and and_7 (out_14, not_1_out, in_2, in_3, not_4_out);
  and and_8 (out_13, D0, in_2, in_3, not_4_out);
  and and_9 (out_12, not_1_out, not_2_out, not_3_out, in_4);
  and and_10 (out_11, D0, not_2_out, not_3_out, in_4);
  and and_11 (out_10, not_1_out, in_2, not_3_out, in_4);
  and and_12 (out_9, D0, in_2, not_3_out, in_4);
  and and_13 (out_8, not_1_out, not_2_out, in_3, in_4);
  and and_14 (out_7, D0, not_2_out, in_3, in_4);
  and and_15 (out_6, not_1_out, in_2, in_3, in_4);
  and and_16 (out_5, D0, in_2, in_3, in_4);
endmodule

module clk (
  input  HALT,
  output DEBUG,
  output out_3
);

  wire clock_1_out, not_1_out;

  Clock clock_1 (.out(clock_1_out));
  and and_1 (DEBUG, clock_1_out, not_1_out);
  not not_1 (not_1_out, HALT);

  assign out_3 = DEBUG;
endmodule

module cte_cu (
  input  [7:0] A_INPUT,
  input  [4:0] INSTRUCTION,
  input  clock,
  output A_IS_ZERO,
  output CTRL,
  output CTRL_1,
  output CTRL_2,
  output CTRL_3,
  output CTRL_4,
  output CTRL_5,
  output CTRL_6,
  output CTRL_7,
  output CTRL_8,
  output CTRL_9,
  output CTRL_10,
  output CTRL_11,
  output CTRL_12,
  output CTRL_13,
  output CTRL_14,
  output CTRL_15,
  output CTRL_16,
  output CTRL_17,
  output CTRL_18,
  output CTRL_19,
  output CTRL_20,
  output CTRL_21,
  output CTRL_22,
  output CTRL_23,
  output CTRL_24,
  output CTRL_25,
  output T,
  output CTRL_26,
  output T_1,
  output CTRL_27,
  output T_2,
  output CTRL_28,
  output T_3,
  output CTRL_29,
  output T_4,
  output CTRL_30,
  output T_5,
  output CTRL_31,
  output T_6,
  output T_7
);

  wire and_1_out, d_ff_1_q, JUMP, nand_1_out, nand_2_out, not_1_out, not_2_out, STEP_RESET;
  wire [3:0] MICROCODE_ROM_data;
  wire [7:5] counter_8_bits_1_o0;

  not not_1 (not_1_out, 1'b1);
  D_Flip_Flop d_ff_1 (.D(STEP_RESET), .clk(not_2_out), .Q(d_ff_1_q), .reset(T));  // open: Qn, preset
  not not_2 (not_2_out, clock);
  nand nand_1 (nand_1_out, A_INPUT[0], A_INPUT[1], A_INPUT[2], A_INPUT[3]);
  nand nand_2 (nand_2_out, A_INPUT[4], A_INPUT[5], A_INPUT[6], A_INPUT[7]);
  and and_1 (and_1_out, d_ff_1_q, not_2_out);
  Counter_8_bits counter_8_bits_1 (
    .COut(1'b1), .CEnable(1'b1), .CWrite(not_1_out), .CReset(and_1_out), .Clock(not_2_out),
    .out_19(counter_8_bits_1_o0[7]), .out_20(counter_8_bits_1_o0[6]), .O0(counter_8_bits_1_o0[5]));  // open: I7, in_7, in_8, in_9, in_10, in_11, in_12, I0, O7, out_15, out_16, out_17, out_18
  and and_2 (A_IS_ZERO, nand_1_out, nand_2_out);
  ROM #(.dataWidth(32)) MICROCODE_ROM (
    .addr({counter_8_bits_1_o0, INSTRUCTION}),
    .data({CTRL, CTRL_1, CTRL_2, CTRL_3, CTRL_4, CTRL_5, CTRL_6, CTRL_7, CTRL_8, CTRL_9, CTRL_10, CTRL_11, CTRL_12, CTRL_13, CTRL_14, CTRL_15, CTRL_16, CTRL_17, CTRL_18, CTRL_19, CTRL_20, CTRL_21, CTRL_22, CTRL_23, CTRL_24, CTRL_25, STEP_RESET, JUMP, MICROCODE_ROM_data}));
  decoder decoder_1 (
    .D0(counter_8_bits_1_o0[5]), .in_2(counter_8_bits_1_o0[6]), .in_3(counter_8_bits_1_o0[7]), .out_13(T_7),
    .out_14(T_6), .out_15(T_5), .out_16(T_4), .out_17(T_3), .out_18(T_2), .out_19(T_1), .out_20(T));  // open: in_4, out_5, out_6, out_7, out_8, out_9, out_10, out_11, out_12
  LedBar ledbar_1 (.led0(T_7), .led1(T_6), .led2(T_5), .led3(T_4), .led4(T_3), .led5(T_2), .led6(T_1), .led7(T));

  // Other names for the same wires on the sheet: OUT_READ = CTRL_25; OUT_WRITE = CTRL_24; IN_READ = CTRL_23;
  //   IN_WRITE = CTRL_22; ADDR_READ = CTRL_21; ADDR_WRITE = CTRL_20; DATA_READ = CTRL_19; DATA_WRITE = CTRL_18;
  //   I_READ = CTRL_17; I_WRITE = CTRL_16; A_READ = CTRL_15; A_WRITE = CTRL_14; Y_READ = CTRL_13; Y_WRITE = CTRL_12;
  //   X_READ = CTRL_11; X_WRITE = CTRL_10; MEM_READ = CTRL_9; MEM_WRITE = CTRL_8; ALU_CTRL2 = CTRL_7;
  //   ALU_CTRL1 = CTRL_6; ALU_CTRL0 = CTRL_5; ALU_EN = CTRL_4; PC_JUMP = CTRL_3; PC_COUNT = CTRL_2; PC_EN = CTRL_1;
  //   HALT = CTRL; T0 = T; T1 = T_1; T2 = T_2; T3 = T_3; T4 = T_4; T5 = T_5; T6 = T_6; T7 = T_7

  // Notes on the sheet:
  //   contents of MICROCODE_ROM (hex, n*v repeats v):
  //   32*40408000 16*20004000 16*0 20000020 80000020 0 0 0 20100020 0 20040020 20010020 28160020 2c160020
  //   2a160020 2b160020 29160020 2d120020 20000000 20000320 200000e0 29*0 40400800 31*0 10030
endmodule

module tce_calc_new (
);

  wire A0, A1, A2, A3, AB, AB0, AB_1, AB_2, AB_3, B0, BA, BA0, BA_2, C, C0, C7, C_1, C_2, C_3, C_4, C_5, C_6,
       C_7, CA, CALC, Cin, Cout, E0, E1, E2, E3, E4, E5, E6, E7, EA0, n7486_3_pin11, SUB, UL, UL0, UR, UR_1,
       UR_2, UR_3;

  _7486 u_7486_1 (
    .pin1(SUB), .pin2(B0), .pin3(BA0), .pin4(SUB), .pin5(B0), .pin6(BA0), .pin13(SUB), .pin12(B0),
    .pin11(BA0), .pin10(SUB), .pin9(Cin), .pin8(CA));
  _7486 u_7486_2 (
    .pin1(SUB), .pin2(B0), .pin3(BA0), .pin4(SUB), .pin5(B0), .pin6(BA0), .pin13(SUB), .pin12(B0),
    .pin11(BA0), .pin10(SUB), .pin9(B0), .pin8(CA));
  _7486 u_7486_3 (
    .pin13(C7), .pin12(SUB), .pin11(n7486_3_pin11), .pin10(SUB), .pin9(B0), .pin8(BA0));  // open: pin1, pin2, pin3, pin4, pin5, pin6
  _7408 u_7408_1 (
    .pin10(n7486_3_pin11), .pin9(CALC), .pin8(Cout));  // open: pin1, pin2, pin3, pin4, pin5, pin6, pin13, pin12, pin11
  _7486 u_7486_4 (
    .pin1(BA0), .pin2(A3), .pin3(AB0), .pin4(BA0), .pin5(A2), .pin6(AB0), .pin13(BA0), .pin12(A1),
    .pin11(AB0), .pin10(BA0), .pin9(A0), .pin8(AB0));
  _7486 u_7486_5 (
    .pin1(BA0), .pin2(A3), .pin3(AB0), .pin4(BA0), .pin5(A2), .pin6(AB0), .pin13(BA0), .pin12(A1),
    .pin11(AB0), .pin10(BA0), .pin9(A0), .pin8(AB0));
  _7408 u_7408_2 (
    .pin1(C0), .pin2(A1), .pin3(UL0), .pin4(CA), .pin5(A0), .pin6(UL0), .pin13(C0), .pin12(A1), .pin11(UL0),
    .pin10(CA), .pin9(A0), .pin8(UL0));
  _7408 u_7408_3 (
    .pin1(C0), .pin2(A1), .pin3(UL0), .pin4(CA), .pin5(A0), .pin6(UL0), .pin13(C0), .pin12(A1), .pin11(UL0),
    .pin10(CA), .pin9(A0), .pin8(UL0));
  _7486 u_7486_6 (
    .pin1(BA_2), .pin2(CA), .pin3(EA0), .pin4(BA), .pin5(CA), .pin6(EA0), .pin13(BA_2), .pin12(CA),
    .pin11(EA0), .pin10(BA), .pin9(CA), .pin8(EA0));
  _7408 u_7408_4 (
    .pin1(C0), .pin2(AB_3), .pin3(UR_3), .pin4(CA), .pin5(AB_1), .pin6(UR_2), .pin13(C0), .pin12(AB_2),
    .pin11(UR_1), .pin10(CA), .pin9(AB), .pin8(UR));
  _7408 u_7408_5 (
    .pin1(C0), .pin2(AB_3), .pin3(UR_3), .pin4(CA), .pin5(AB_1), .pin6(UR_2), .pin13(C0), .pin12(AB_2),
    .pin11(UR_1), .pin10(CA), .pin9(AB), .pin8(UR));
  _7432 u_7432_1 (
    .pin1(UR), .pin2(UL), .pin3(C_3), .pin4(UR), .pin5(UL), .pin6(C_2), .pin13(UR), .pin12(UL), .pin11(C_1),
    .pin10(UR), .pin9(UL), .pin8(C));
  _7432 u_7432_2 (
    .pin1(UR), .pin2(UL), .pin3(C_7), .pin4(UR), .pin5(UL), .pin6(C_6), .pin13(UR), .pin12(UL), .pin11(C_5),
    .pin10(UR), .pin9(UL), .pin8(C_4));
  _7408 u_7408_6 (
    .pin1(CALC), .pin2(EA0), .pin3(E3), .pin4(CALC), .pin5(EA0), .pin6(E2), .pin13(CALC), .pin12(EA0),
    .pin11(E1), .pin10(CALC), .pin9(EA0), .pin8(E0));
  _7408 u_7408_7 (
    .pin1(CALC), .pin2(EA0), .pin3(E7), .pin4(CALC), .pin5(EA0), .pin6(E6), .pin13(CALC), .pin12(EA0),
    .pin11(E5), .pin10(CALC), .pin9(EA0), .pin8(E4));
endmodule

module alu_not (
  input  A7,
  input  A6,
  input  in_3,
  input  in_4,
  input  in_5,
  input  in_6,
  input  in_7,
  input  A0,
  input  en,
  output out_10,
  output out_11,
  output out_12,
  output out_13,
  output out_14,
  output out_15,
  output out_16,
  output out_17
);

  wire n7404_1_pin2, n7404_1_pin8, n7404_1_pin10, n7404_1_pin12, n7404_2_pin8, n7404_2_pin10, n7404_2_pin12;

  _7404 u_7404_1 (
    .pin1(in_5), .pin2(n7404_1_pin2), .pin13(in_6), .pin12(n7404_1_pin12), .pin11(in_7),
    .pin10(n7404_1_pin10), .pin9(A0), .pin8(n7404_1_pin8));  // open: pin3, pin4, pin5, pin6
  _7404 u_7404_2 (
    .pin1(A7), .pin2(en), .pin13(A6), .pin12(n7404_2_pin12), .pin11(in_3), .pin10(n7404_2_pin10),
    .pin9(in_4), .pin8(n7404_2_pin8));  // open: pin3, pin4, pin5, pin6
  bus_transceiver bus_transceiver_1 (
    .in_1(n7404_1_pin8), .in_2(n7404_1_pin8), .in_3(n7404_1_pin10), .in_4(n7404_1_pin12),
    .in_5(n7404_1_pin2), .in_6(n7404_2_pin8), .in_7(n7404_2_pin10), .in_8(n7404_2_pin12), .enable(en),
    .out_11(n7404_1_pin8), .out_12(n7404_1_pin10), .out_13(n7404_1_pin12), .out_14(n7404_1_pin2),
    .out_15(n7404_2_pin8), .out_16(n7404_2_pin10), .out_17(n7404_2_pin12));  // open: out_10

  // Other names for the same wires on the sheet: A1 = in_7; A2 = in_6; A3 = in_5; A4 = in_4; A5 = in_3; OR = en

  // Notes on the sheet:
  //   A0: pull=up
  //   AND
endmodule

module register_old (
  input  D0,
  input  in_2,
  input  in_3,
  input  in_4,
  input  in_5,
  input  in_6,
  input  in_7,
  input  D7,
  input  en_input,
  input  clock,
  input  en_output,
  output out_12,
  output out_13,
  output out_14,
  output out_15,
  output out_16,
  output out_17,
  output out_18,
  output out_19,
  output Q0,
  output out_21,
  output out_22,
  output out_23,
  output out_24,
  output out_25,
  output out_26,
  output Q7
);

  Register L_8bitregister_9b5b12da (
    .D({D7, in_7, in_6, in_5, in_4, in_3, in_2, D0}), .en(en_input), .clk(clock),
    .Q({out_12, out_13, out_14, out_15, out_16, out_17, out_18, out_19}));  // open: clr
  assign {Q7, out_26, out_25, out_24, out_23, out_22, out_21, Q0} = en_output ? {out_12, out_13, out_14, out_15, out_16, out_17, out_18, out_19} : 8'bz;  // Controlled_Buffer controlled_buffer_1
endmodule

module twobitadder (
  input  A0,
  input  B0,
  input  A1,
  input  B1,
  input  Cin,
  output Cout,
  output E0,
  output E1
);

  wire C0, n7408_1_pin3, n7408_1_pin6, n7408_1_pin8, n7408_1_pin11, n7486_1_pin1, n7486_1_pin5;

  _7486 u_7486_1 (
    .pin1(n7486_1_pin1), .pin2(C0), .pin3(E1), .pin4(Cin), .pin5(n7486_1_pin5), .pin6(E0), .pin13(B1),
    .pin12(A1), .pin11(n7486_1_pin1), .pin10(B0), .pin9(A0), .pin8(n7486_1_pin5));
  _7408 u_7408_1 (
    .pin1(n7486_1_pin1), .pin2(C0), .pin3(n7408_1_pin3), .pin4(n7486_1_pin5), .pin5(Cin),
    .pin6(n7408_1_pin6), .pin13(A1), .pin12(B1), .pin11(n7408_1_pin11), .pin10(A0), .pin9(B0),
    .pin8(n7408_1_pin8));
  _7432 u_7432_1 (
    .pin13(n7408_1_pin11), .pin12(n7408_1_pin3), .pin11(Cout), .pin10(n7408_1_pin6), .pin9(n7408_1_pin8),
    .pin8(C0));  // open: pin1, pin2, pin3, pin4, pin5, pin6
endmodule

module tce_alu_old (
  input  A7,
  input  A6,
  input  in_3,
  input  in_4,
  input  in_5,
  input  in_6,
  input  in_7,
  input  A0,
  input  B0,
  input  B1,
  input  in_11,
  input  in_12,
  input  in_13,
  input  in_14,
  input  in_15,
  input  B7,
  input  Cin,
  input  clock,
  input  alu_out,
  input  CTRL0,
  input  CTRL1,
  input  CTRL2,
  output out_23,
  output out_24,
  output out_25,
  output out_26,
  output out_27,
  output out_28,
  output out_29,
  output out_30,
  output Cout
);

  wire alu_and_1_p4, alu_and_1_p5, alu_and_1_p6, alu_and_1_p7, alu_and_1_p8, alu_and_1_p9, alu_and_1_p10,
       alu_and_1_p11, alu_calc_1_p4, alu_calc_1_p5, alu_calc_1_p6, alu_calc_1_p7, alu_calc_1_p8,
       alu_calc_1_p9, alu_calc_1_p10, alu_calc_1_p11, alu_decoder_1_add, alu_decoder_1_and,
       alu_decoder_1_sub, alu_decoder_1_xor, alu_or_1_p4, alu_or_1_p5, alu_or_1_p6, alu_or_1_p7, alu_or_1_p8,
       alu_or_1_p9, alu_or_1_p10, alu_or_1_p11, alu_xor_1_p4, alu_xor_1_p5, alu_xor_1_p6, alu_xor_1_p7,
       alu_xor_1_p8, alu_xor_1_p9, alu_xor_1_p10, alu_xor_1_p11;

  alu_decoder alu_decoder_1 (
    .ADD(alu_decoder_1_add), .SUb(alu_decoder_1_sub), .AND(alu_decoder_1_and), .OR(in_11),
    .XOR(alu_decoder_1_xor), .CTRL0(CTRL0), .CTRL1(CTRL1), .CTRL2(CTRL2));  // open: O_NOT
  // alu_calc alu_calc_1: pin names not known; wires that end beside it: in_6, in_7, A0, alu_calc_1_p4, alu_calc_1_p5, alu_calc_1_p6, alu_calc_1_p7, alu_calc_1_p8, alu_calc_1_p9, alu_calc_1_p10, alu_calc_1_p11, Cout, B1, in_11, in_12, in_13, in_14, in_14, alu_calc_1_p11, alu_calc_1_p11, alu_calc_1_p11, alu_calc_1_p11, alu_calc_1_p11, alu_calc_1_p11, alu_calc_1_p11, B0, B1, B1
  // alu_and alu_and_1: pin names not known; wires that end beside it: in_6, in_7, A0, alu_and_1_p4, alu_and_1_p5, alu_and_1_p6, alu_and_1_p7, alu_and_1_p8, alu_and_1_p9, alu_and_1_p10, alu_and_1_p11, B0, B1, in_11, in_12, in_13, in_14, in_15, B7, alu_and_1_p9, alu_and_1_p9, alu_and_1_p9, alu_and_1_p9, alu_and_1_p9, alu_and_1_p10, alu_and_1_p11, B0
  // alu_or alu_or_1: pin names not known; wires that end beside it: in_6, in_7, A0, alu_or_1_p4, alu_or_1_p5, alu_or_1_p6, alu_or_1_p7, alu_or_1_p8, alu_or_1_p9, alu_or_1_p10, alu_or_1_p11, B0, B1, in_11, in_12, in_13, in_14, in_15, alu_or_1_p10, alu_or_1_p10, alu_or_1_p10, alu_or_1_p10, alu_or_1_p10, alu_or_1_p10, alu_or_1_p11, B7, A7
  // alu_xor alu_xor_1: pin names not known; wires that end beside it: in_6, in_7, A0, alu_xor_1_p4, alu_xor_1_p5, alu_xor_1_p6, alu_xor_1_p7, alu_xor_1_p8, alu_xor_1_p9, alu_xor_1_p10, alu_xor_1_p11
  alu_output_controller alu_output_controller_1 (
    .O0(out_23), .O1(out_24), .O2(out_25), .O3(out_26), .O4(out_27), .O5(out_28), .O6(out_29), .O7(out_30),
    .alu_out(alu_out), .clock(clock), .in_4(alu_calc_1_p7), .in_5(alu_calc_1_p8), .in_6(alu_calc_1_p9),
    .in_7(alu_calc_1_p10), .E7(alu_calc_1_p11), .N0(alu_and_1_p4), .E0(alu_calc_1_p4), .in_10(alu_and_1_p5),
    .in_11(alu_and_1_p6), .in_12(alu_and_1_p7), .in_13(alu_and_1_p8), .in_14(alu_and_1_p9),
    .N(alu_and_1_p10), .N7(alu_and_1_p11), .V0(alu_or_1_p4), .in_18(alu_or_1_p5), .in_19(alu_or_1_p6),
    .E(alu_calc_1_p5), .in_20(alu_or_1_p7), .in_21(alu_or_1_p8), .in_22(alu_or_1_p9), .V(alu_or_1_p10),
    .V7(alu_or_1_p11), .X0(alu_xor_1_p4), .in_26(alu_xor_1_p5), .in_27(alu_xor_1_p6), .in_28(alu_xor_1_p7),
    .in_3(alu_calc_1_p6), .in_29(alu_xor_1_p8), .X(alu_xor_1_p9), .in_31(alu_xor_1_p10), .X7(alu_xor_1_p11));

  // Notes on the sheet:
  //   FUNCTION DECODER
endmodule

module bus_transceiver (
  input  in_1,
  input  in_2,
  input  in_3,
  input  in_4,
  input  in_5,
  input  in_6,
  input  in_7,
  input  in_8,
  input  enable,
  output out_10,
  output out_11,
  output out_12,
  output out_13,
  output out_14,
  output out_15,
  output out_16,
  output out_17
);

  assign out_10 = enable ? in_1 : 1'bz;  // Controlled_Buffer controlled_buffer_1
  assign out_11 = enable ? in_2 : 1'bz;  // Controlled_Buffer controlled_buffer_2
  assign out_12 = enable ? in_3 : 1'bz;  // Controlled_Buffer controlled_buffer_3
  assign out_13 = enable ? in_4 : 1'bz;  // Controlled_Buffer controlled_buffer_4
  assign out_14 = enable ? in_5 : 1'bz;  // Controlled_Buffer controlled_buffer_5
  assign out_15 = enable ? in_6 : 1'bz;  // Controlled_Buffer controlled_buffer_6
  assign out_16 = enable ? in_7 : 1'bz;  // Controlled_Buffer controlled_buffer_7
  assign out_17 = enable ? in_8 : 1'bz;  // Controlled_Buffer controlled_buffer_8
endmodule

module tce (
  input  IN7,
  input  in_2,
  input  in_3,
  input  in_4,
  input  in_5,
  input  in_6,
  input  in_7,
  input  IN0,
  output O7,
  output out_10,
  output out_11,
  output out_12,
  output out_13,
  output out_14,
  output out_15,
  output O0
);

  wire button_1_out, clk_1_debug, cte_cu_1_a_is_zero, cte_cu_1_ctrl, cte_cu_1_ctrl_1, cte_cu_1_ctrl_2,
       cte_cu_1_ctrl_3, cte_cu_1_ctrl_4, cte_cu_1_ctrl_5, cte_cu_1_ctrl_6, cte_cu_1_ctrl_7, cte_cu_1_ctrl_10,
       cte_cu_1_ctrl_11, cte_cu_1_ctrl_12, cte_cu_1_ctrl_13, cte_cu_1_ctrl_14, cte_cu_1_ctrl_15,
       cte_cu_1_ctrl_17, cte_cu_1_ctrl_18, cte_cu_1_ctrl_19, cte_cu_1_ctrl_20, cte_cu_1_ctrl_21,
       cte_cu_1_ctrl_22, cte_cu_1_ctrl_23, cte_cu_1_ctrl_24, cte_cu_1_ctrl_25, cte_cu_1_ctrl_26,
       cte_cu_1_ctrl_27, cte_cu_1_ctrl_28, cte_cu_1_ctrl_29, cte_cu_1_ctrl_30, cte_cu_1_ctrl_31, cte_cu_1_t,
       cte_cu_1_t_1, cte_cu_1_t_2, cte_cu_1_t_3, cte_cu_1_t_4, cte_cu_1_t_5, cte_cu_1_t_6, cte_cu_1_t_7,
       mem_new_big_1_p22, mem_new_big_1_p24, mem_new_big_1_p25, pc_1_out_7, pc_1_out_8, pc_1_out_9,
       pc_1_out_10, pc_1_out_11, pc_1_out_12, pc_1_out_13, pc_1_out_14, register_1_dg0, register_1_out_12,
       register_1_out_13, register_1_out_14, register_1_out_15, register_1_out_16, register_1_out_17,
       register_1_out_18, register_2_dg0, register_2_out_12, register_2_out_13, register_2_out_14,
       register_2_out_15, register_2_out_16, register_2_out_17, register_2_out_18, register_3_dg0,
       register_3_out_12, register_3_out_13, register_3_out_14, register_3_out_15, register_3_out_16,
       register_3_out_17, register_3_out_18, register_4_dg0, register_4_out_12, register_4_out_13,
       register_4_out_14, register_4_out_15, register_4_out_16, register_4_out_17, register_4_out_18,
       register_5_dg0, register_5_out_12, register_5_out_13, register_5_out_14, register_5_out_15,
       register_5_out_16, register_5_out_17, register_5_out_18, register_6_dg0, register_6_out_12,
       register_6_out_13, register_6_out_14, register_6_out_15, register_6_out_16, register_6_out_17,
       register_6_out_18, register_7_dg0, register_7_out_12, register_7_out_13, register_7_out_14,
       register_7_out_15, register_7_out_16, register_7_out_17, register_7_out_18, register_8_dg0,
       register_8_out_12, register_8_out_13, register_8_out_14, register_8_out_15, register_8_out_16,
       register_8_out_17, register_8_out_18;
  wire [4:0] register_1_q0;
  wire [5:5] mem_new_big_1_p23;
  wire [7:0] pc_1_o, register_2_q0, undriven;

  LedBar ledbar_1 (
    .led0(pc_1_o[7]), .led1(pc_1_o[6]), .led2(pc_1_o[5]), .led3(pc_1_o[4]), .led4(pc_1_o[3]),
    .led5(pc_1_o[2]), .led6(pc_1_o[1]), .led7(pc_1_o[0]));
  LedBar #(.matrixcols(1)) ledbar_2 (.led0(register_2_q0[3]));
  LedBar ledbar_3 (
    .led0(register_2_q0[7]), .led1(register_2_q0[6]), .led2(register_2_q0[5]), .led3(register_2_q0[4]),
    .led4(register_2_q0[3]), .led5(register_2_q0[2]), .led6(register_2_q0[1]), .led7(register_2_q0[0]));
  LED led_1 (.in(clk_1_debug));
  clk clk_1 (.DEBUG(clk_1_debug), .out_3(register_2_q0[3]), .HALT(cte_cu_1_ctrl));
  pc pc_1 (
    .out_7(pc_1_out_7), .out_8(pc_1_out_8), .out_9(pc_1_out_9), .out_10(pc_1_out_10), .out_11(pc_1_out_11),
    .out_12(pc_1_out_12), .out_13(pc_1_out_13), .out_14(pc_1_out_14), .O(pc_1_o), .clock(register_2_q0[3]),
    .enabled(cte_cu_1_ctrl_1), .A(pc_1_o), .reset(button_1_out), .jump(cte_cu_1_ctrl_3),
    .count(cte_cu_1_ctrl_2));
  LedBar ledbar_4 (
    .led0(pc_1_out_7), .led1(pc_1_out_8), .led2(pc_1_out_9), .led3(pc_1_out_10), .led4(pc_1_out_11),
    .led5(pc_1_out_12), .led6(pc_1_out_13), .led7(pc_1_out_14));
  LedBar ledbar_5 (
    .led0(register_1_out_12), .led1(register_1_out_13), .led2(register_1_out_14), .led3(register_1_out_15),
    .led4(register_1_out_16), .led5(register_1_out_17), .led6(register_1_out_18), .led7(register_1_dg0));
  register register_1 (
    .Q0(register_1_q0[0]), .Q1(register_1_q0[1]), .Q2(register_1_q0[2]), .Q3(register_1_q0[3]),
    .Q4(register_1_q0[4]), .out_12(register_1_out_12), .out_13(register_1_out_13),
    .out_14(register_1_out_14), .out_15(register_1_out_15), .out_16(register_1_out_16),
    .out_17(register_1_out_17), .out_18(register_1_out_18), .DG0(register_1_dg0),
    .en_input(mem_new_big_1_p22), .clock(register_2_q0[3]), .D0(register_2_q0[0]), .D1(register_2_q0[1]),
    .D2(register_2_q0[2]), .D3(register_2_q0[3]), .D4(register_2_q0[4]), .D5(register_2_q0[5]),
    .D6(register_2_q0[6]), .D7(register_2_q0[7]), .en_output(1'b1));  // open: Q5, Q6, Q7
  LedBar ledbar_6 (
    .led0(register_2_out_12), .led1(register_2_out_13), .led2(register_2_out_14), .led3(register_2_out_15),
    .led4(register_2_out_16), .led5(register_2_out_17), .led6(register_2_out_18), .led7(register_2_dg0));
  register register_2 (
    .Q0(register_2_q0[0]), .Q1(register_2_q0[1]), .Q2(register_2_q0[2]), .Q3(register_2_q0[3]),
    .Q4(register_2_q0[4]), .Q5(register_2_q0[5]), .Q6(register_2_q0[6]), .Q7(register_2_q0[7]),
    .out_12(register_2_out_12), .out_13(register_2_out_13), .out_14(register_2_out_14),
    .out_15(register_2_out_15), .out_16(register_2_out_16), .out_17(register_2_out_17),
    .out_18(register_2_out_18), .DG0(register_2_dg0), .en_input(cte_cu_1_ctrl_22), .clock(register_2_q0[3]),
    .D0(IN0), .D1(in_7), .D2(in_6), .D3(in_5), .D4(in_4), .D5(in_3), .D6(in_2), .D7(IN7),
    .en_output(cte_cu_1_ctrl_23));
  LedBar ledbar_7 (
    .led0(register_3_out_12), .led1(register_3_out_13), .led2(register_3_out_14), .led3(register_3_out_15),
    .led4(register_3_out_16), .led5(register_3_out_17), .led6(register_3_out_18), .led7(register_3_dg0));
  register register_3 (
    .Q0(O0), .Q1(out_15), .Q2(out_14), .Q3(out_13), .Q4(out_12), .Q5(out_11), .Q6(out_10), .Q7(O7),
    .out_12(register_3_out_12), .out_13(register_3_out_13), .out_14(register_3_out_14),
    .out_15(register_3_out_15), .out_16(register_3_out_16), .out_17(register_3_out_17),
    .out_18(register_3_out_18), .DG0(register_3_dg0), .en_input(cte_cu_1_ctrl_24), .clock(register_2_q0[3]),
    .D0(register_2_q0[0]), .D1(register_2_q0[1]), .D2(register_2_q0[2]), .D3(register_2_q0[3]),
    .D4(register_2_q0[4]), .D5(register_2_q0[5]), .D6(register_2_q0[6]), .D7(register_2_q0[7]),
    .en_output(cte_cu_1_ctrl_25));
  Button button_1 (.out(button_1_out));
  LedBar ledbar_8 (
    .led0(register_4_out_12), .led1(register_4_out_13), .led2(register_4_out_14), .led3(register_4_out_15),
    .led4(register_4_out_16), .led5(register_4_out_17), .led6(register_4_out_18), .led7(register_4_dg0));
  register register_4 (
    .Q0(register_2_q0[0]), .Q1(register_2_q0[1]), .Q2(register_2_q0[2]), .Q3(register_2_q0[3]),
    .Q4(register_2_q0[4]), .Q5(register_2_q0[5]), .Q6(register_2_q0[6]), .Q7(register_2_q0[7]),
    .out_12(register_4_out_12), .out_13(register_4_out_13), .out_14(register_4_out_14),
    .out_15(register_4_out_15), .out_16(register_4_out_16), .out_17(register_4_out_17),
    .out_18(register_4_out_18), .DG0(register_4_dg0), .en_input(cte_cu_1_ctrl_10), .clock(register_2_q0[3]),
    .D0(register_2_q0[0]), .D1(register_2_q0[1]), .D2(register_2_q0[2]), .D3(register_2_q0[3]),
    .D4(register_2_q0[4]), .D5(register_2_q0[5]), .D6(register_2_q0[6]), .D7(register_2_q0[7]),
    .en_output(cte_cu_1_ctrl_11));
  // mem_new_big mem_new_big_1: pin names not known; wires that end beside it: register_2_q0[0], register_2_q0[1], register_2_q0[2], register_2_q0[3], register_2_q0[4], register_2_q0[6], register_2_q0[7], register_2_q0[0], register_2_q0[1], register_2_q0[2], register_2_q0[3], register_2_q0[4], register_2_q0[5], register_2_q0[6], register_2_q0[7], register_2_q0[5], register_2_q0[3], pc_1_o[1], pc_1_o[3], pc_1_o[5], pc_1_o[7], mem_new_big_1_p22, mem_new_big_1_p23[5], mem_new_big_1_p24, mem_new_big_1_p25
  alu alu_1 (
    .X(register_2_q0), .Y(register_2_q0), .A(undriven), .CLOCK(register_2_q0[3]), .ALU_EN(cte_cu_1_ctrl_4),
    .ALU_CTRL0(cte_cu_1_ctrl_5), .ALU_CTRL1(cte_cu_1_ctrl_6), .ALU_CTRL2(cte_cu_1_ctrl_7));  // open: CARRY_IN, CARRY_OUT
  LedBar ledbar_9 (
    .led0(register_5_out_12), .led1(register_5_out_13), .led2(register_5_out_14), .led3(register_5_out_15),
    .led4(register_5_out_16), .led5(register_5_out_17), .led6(register_5_out_18), .led7(register_5_dg0));
  LedBar ledbar_10 (
    .led0(register_6_out_12), .led1(register_6_out_13), .led2(register_6_out_14), .led3(register_6_out_15),
    .led4(register_6_out_16), .led5(register_6_out_17), .led6(register_6_out_18), .led7(register_6_dg0));
  LedBar ledbar_11 (
    .led0(register_7_out_12), .led1(register_7_out_13), .led2(register_7_out_14), .led3(register_7_out_15),
    .led4(register_7_out_16), .led5(register_7_out_17), .led6(register_7_out_18), .led7(register_7_dg0));
  LedBar ledbar_12 (
    .led0(register_8_out_12), .led1(register_8_out_13), .led2(register_8_out_14), .led3(register_8_out_15),
    .led4(register_8_out_16), .led5(register_8_out_17), .led6(register_8_out_18), .led7(register_8_dg0));
  register register_5 (
    .Q0(register_2_q0[0]), .Q1(register_2_q0[1]), .Q2(register_2_q0[2]), .Q3(register_2_q0[3]),
    .Q4(register_2_q0[4]), .Q5(register_2_q0[5]), .Q6(register_2_q0[6]), .Q7(register_2_q0[7]),
    .out_12(register_5_out_12), .out_13(register_5_out_13), .out_14(register_5_out_14),
    .out_15(register_5_out_15), .out_16(register_5_out_16), .out_17(register_5_out_17),
    .out_18(register_5_out_18), .DG0(register_5_dg0), .en_input(cte_cu_1_ctrl_18), .clock(register_2_q0[3]),
    .D0(register_2_q0[0]), .D1(register_2_q0[1]), .D2(register_2_q0[2]), .D3(register_2_q0[3]),
    .D4(register_2_q0[4]), .D5(register_2_q0[5]), .D6(register_2_q0[6]), .D7(register_2_q0[7]),
    .en_output(cte_cu_1_ctrl_19));
  register register_6 (
    .Q0(pc_1_o[0]), .Q1(pc_1_o[1]), .Q2(pc_1_o[2]), .Q3(pc_1_o[3]), .Q4(pc_1_o[4]), .Q5(pc_1_o[5]),
    .Q6(pc_1_o[6]), .Q7(pc_1_o[7]), .out_12(register_6_out_12), .out_13(register_6_out_13),
    .out_14(register_6_out_14), .out_15(register_6_out_15), .out_16(register_6_out_16),
    .out_17(register_6_out_17), .out_18(register_6_out_18), .DG0(register_6_dg0),
    .en_input(cte_cu_1_ctrl_20), .clock(register_2_q0[3]), .D0(register_2_q0[0]), .D1(register_2_q0[1]),
    .D2(register_2_q0[2]), .D3(register_2_q0[3]), .D4(register_2_q0[4]), .D5(register_2_q0[5]),
    .D6(register_2_q0[6]), .D7(register_2_q0[7]), .en_output(cte_cu_1_ctrl_21));
  register register_7 (
    .Q0(register_2_q0[0]), .Q1(register_2_q0[1]), .Q2(register_2_q0[2]), .Q3(register_2_q0[3]),
    .Q4(register_2_q0[4]), .Q5(register_2_q0[5]), .Q6(register_2_q0[6]), .Q7(register_2_q0[7]),
    .out_12(register_7_out_12), .out_13(register_7_out_13), .out_14(register_7_out_14),
    .out_15(register_7_out_15), .out_16(register_7_out_16), .out_17(register_7_out_17),
    .out_18(register_7_out_18), .DG0(register_7_dg0), .en_input(cte_cu_1_ctrl_12), .clock(register_2_q0[3]),
    .D0(register_2_q0[0]), .D1(register_2_q0[1]), .D2(register_2_q0[2]), .D3(register_2_q0[3]),
    .D4(register_2_q0[4]), .D5(register_2_q0[5]), .D6(register_2_q0[6]), .D7(register_2_q0[7]),
    .en_output(cte_cu_1_ctrl_13));
  register register_8 (
    .Q0(register_2_q0[0]), .Q1(register_2_q0[1]), .Q2(register_2_q0[2]), .Q3(register_2_q0[3]),
    .Q4(register_2_q0[4]), .Q5(register_2_q0[5]), .Q6(register_2_q0[6]), .Q7(register_2_q0[7]),
    .out_12(register_8_out_12), .out_13(register_8_out_13), .out_14(register_8_out_14),
    .out_15(register_8_out_15), .out_16(register_8_out_16), .out_17(register_8_out_17),
    .out_18(register_8_out_18), .DG0(register_8_dg0), .en_input(cte_cu_1_ctrl_14), .clock(register_2_q0[3]),
    .D0(undriven[0]), .D1(undriven[1]), .D2(undriven[2]), .D3(undriven[3]), .D4(undriven[4]),
    .D5(undriven[5]), .D6(undriven[6]), .D7(undriven[7]), .en_output(cte_cu_1_ctrl_15));
  LedBar #(.matrixcols(32)) ledbar_13 (
    .led0(cte_cu_1_ctrl), .led1(cte_cu_1_ctrl_1), .led2(cte_cu_1_ctrl_2), .led3(cte_cu_1_ctrl_3),
    .led4(cte_cu_1_ctrl_4), .led5(cte_cu_1_ctrl_5), .led6(cte_cu_1_ctrl_6), .led7(cte_cu_1_ctrl_7),
    .led8(mem_new_big_1_p24), .led9(mem_new_big_1_p25), .led10(cte_cu_1_ctrl_10), .led11(cte_cu_1_ctrl_11),
    .led12(cte_cu_1_ctrl_12), .led13(cte_cu_1_ctrl_13), .led14(cte_cu_1_ctrl_14), .led15(cte_cu_1_ctrl_15),
    .led16(mem_new_big_1_p22), .led17(cte_cu_1_ctrl_17), .led18(cte_cu_1_ctrl_18), .led19(cte_cu_1_ctrl_19),
    .led20(cte_cu_1_ctrl_20), .led21(cte_cu_1_ctrl_21), .led22(cte_cu_1_ctrl_22), .led23(cte_cu_1_ctrl_23),
    .led24(cte_cu_1_ctrl_24), .led25(cte_cu_1_ctrl_25), .led26(cte_cu_1_ctrl_26), .led27(cte_cu_1_ctrl_27),
    .led28(cte_cu_1_ctrl_28), .led29(cte_cu_1_ctrl_29), .led30(cte_cu_1_ctrl_30), .led31(cte_cu_1_ctrl_31));
  cte_cu cte_cu_1 (
    .T(cte_cu_1_t), .T_1(cte_cu_1_t_1), .T_2(cte_cu_1_t_2), .T_3(cte_cu_1_t_3), .T_4(cte_cu_1_t_4),
    .T_5(cte_cu_1_t_5), .T_6(cte_cu_1_t_6), .T_7(cte_cu_1_t_7), .CTRL(cte_cu_1_ctrl),
    .CTRL_1(cte_cu_1_ctrl_1), .CTRL_2(cte_cu_1_ctrl_2), .CTRL_3(cte_cu_1_ctrl_3), .CTRL_4(cte_cu_1_ctrl_4),
    .CTRL_5(cte_cu_1_ctrl_5), .CTRL_6(cte_cu_1_ctrl_6), .CTRL_7(cte_cu_1_ctrl_7), .CTRL_8(mem_new_big_1_p24),
    .CTRL_9(mem_new_big_1_p25), .CTRL_10(cte_cu_1_ctrl_10), .CTRL_11(cte_cu_1_ctrl_11),
    .CTRL_12(cte_cu_1_ctrl_12), .CTRL_13(cte_cu_1_ctrl_13), .CTRL_14(cte_cu_1_ctrl_14),
    .CTRL_15(cte_cu_1_ctrl_15), .CTRL_16(mem_new_big_1_p22), .CTRL_17(cte_cu_1_ctrl_17),
    .CTRL_18(cte_cu_1_ctrl_18), .CTRL_19(cte_cu_1_ctrl_19), .CTRL_20(cte_cu_1_ctrl_20),
    .CTRL_21(cte_cu_1_ctrl_21), .CTRL_22(cte_cu_1_ctrl_22), .CTRL_23(cte_cu_1_ctrl_23),
    .CTRL_24(cte_cu_1_ctrl_24), .CTRL_25(cte_cu_1_ctrl_25), .CTRL_26(cte_cu_1_ctrl_26),
    .CTRL_27(cte_cu_1_ctrl_27), .CTRL_28(cte_cu_1_ctrl_28), .CTRL_29(cte_cu_1_ctrl_29),
    .CTRL_30(cte_cu_1_ctrl_30), .CTRL_31(cte_cu_1_ctrl_31), .A_IS_ZERO(cte_cu_1_a_is_zero),
    .clock(register_2_q0[3]), .A_INPUT(register_2_q0), .INSTRUCTION(register_1_q0));
  LedBar #(.matrixcols(1)) ledbar_14 (.led0(cte_cu_1_a_is_zero));
  LedBar ledbar_15 (
    .led0(cte_cu_1_t_7), .led1(cte_cu_1_t_6), .led2(cte_cu_1_t_5), .led3(cte_cu_1_t_4), .led4(cte_cu_1_t_3),
    .led5(cte_cu_1_t_2), .led6(cte_cu_1_t_1), .led7(cte_cu_1_t));

  // Notes on the sheet:
  //   ADDRESS BUS
  //   CLOCK
  //   DATA BUS
  //   7
  //   4
  //   INSTRUCTION REGISTER
  //   8
  //   1
  //   5
  //   6
  //   2
  //   3
  //   CONTROL BUS
endmodule

module memory_old (
  input  A7,
  input  in_2,
  input  in_3,
  input  in_4,
  input  in_5,
  input  in_6,
  input  in_7,
  input  A0,
  input  D0,
  input  in_10,
  input  in_11,
  input  in_12,
  input  in_13,
  input  in_14,
  input  in_15,
  input  D7,
  input  clock,
  input  en_read,
  input  en_write,
  input  in_20,
  input  in_21,
  input  in_22,
  input  in_23,
  input  in_24,
  input  in_25,
  input  in_26,
  input  in_27,
  input  in_28,
  input  in_29,
  input  in_30,
  input  in_31,
  input  in_32,
  input  in_33,
  input  in_34,
  input  in_35,
  input  in_36,
  input  in_37,
  input  in_38,
  output Q0,
  output out_40,
  output out_41,
  output out_42,
  output out_43,
  output out_44,
  output out_45,
  output Q7,
  output out_47,
  output out_48,
  output out_49,
  output out_50,
  output out_51,
  output out_52,
  output out_53,
  output out_54
);

  wire and_1_out, and_2_out, and_3_out, and_4_out, and_5_out, and_6_out, and_7_out, and_8_out,
       decoder_1_out_17, decoder_1_out_18, decoder_1_out_19, decoder_1_out_20;
  wire [7:0] ram_1_dout;

  RAM ram_1 (
    .addr({A7, in_2, in_3, in_4, in_5, in_6, in_7, A0}), .we(en_write), .oe(en_read), .clk(clock),
    .din({D7, in_15, in_14, in_13, in_12, in_11, in_10, D0}), .dout(ram_1_dout));
  and and_1 (and_1_out, decoder_1_out_20, in_38);
  and and_2 (and_2_out, decoder_1_out_20, in_36);
  register register_1 (
    .Q0(out_47), .Q1(out_48), .Q2(out_49), .Q3(out_50), .Q4(out_51), .Q5(out_52), .Q6(out_53), .Q7(out_54),
    .en_input(and_1_out), .clock(in_37), .D0(in_28), .D1(in_29), .D2(in_30), .D3(in_31), .D4(in_32),
    .D5(in_33), .D6(in_34), .D7(in_35), .en_output(and_2_out));  // open: out_12, out_13, out_14, out_15, out_16, out_17, out_18, DG0
  and and_3 (and_3_out, decoder_1_out_19, in_38);
  and and_4 (and_4_out, decoder_1_out_19, in_36);
  register register_2 (
    .Q0(out_47), .Q1(out_48), .Q2(out_49), .Q3(out_50), .Q4(out_51), .Q5(out_52), .Q6(out_53), .Q7(out_54),
    .en_input(and_3_out), .clock(in_37), .D0(in_28), .D1(in_29), .D2(in_30), .D3(in_31), .D4(in_32),
    .D5(in_33), .D6(in_34), .D7(in_35), .en_output(and_4_out));  // open: out_12, out_13, out_14, out_15, out_16, out_17, out_18, DG0
  decoder decoder_1 (
    .D0(in_27), .in_2(in_26), .out_17(decoder_1_out_17), .out_18(decoder_1_out_18),
    .out_19(decoder_1_out_19), .out_20(decoder_1_out_20));  // open: in_3, in_4, out_5, out_6, out_7, out_8, out_9, out_10, out_11, out_12, out_13, out_14, out_15, out_16
  register register_3 (
    .Q0(out_47), .Q1(out_48), .Q2(out_49), .Q3(out_50), .Q4(out_51), .Q5(out_52), .Q6(out_53), .Q7(out_54),
    .en_input(and_5_out), .clock(in_37), .D0(in_28), .D1(in_29), .D2(in_30), .D3(in_31), .D4(in_32),
    .D5(in_33), .D6(in_34), .D7(in_35), .en_output(and_6_out));  // open: out_12, out_13, out_14, out_15, out_16, out_17, out_18, DG0
  register register_4 (
    .Q0(out_47), .Q1(out_48), .Q2(out_49), .Q3(out_50), .Q4(out_51), .Q5(out_52), .Q6(out_53), .Q7(out_54),
    .en_input(and_7_out), .clock(in_37), .D0(in_28), .D1(in_29), .D2(in_30), .D3(in_31), .D4(in_32),
    .D5(in_33), .D6(in_34), .D7(in_35), .en_output(and_8_out));  // open: out_12, out_13, out_14, out_15, out_16, out_17, out_18, DG0
  and and_5 (and_5_out, decoder_1_out_18, in_38);
  and and_6 (and_6_out, decoder_1_out_18, in_36);
  and and_7 (and_7_out, decoder_1_out_17, in_38);
  and and_8 (and_8_out, decoder_1_out_17, in_36);
  assign {Q7, out_45, out_44, out_43, out_42, out_41, out_40, Q0} = en_read ? ram_1_dout : 8'bz;  // Controlled_Buffer controlled_buffer_1
endmodule

module Counter_8_bits (
  input  COut,
  input  CEnable,
  input  CWrite,
  input  CReset,
  input  Clock,
  input  I7,
  input  in_7,
  input  in_8,
  input  in_9,
  input  in_10,
  input  in_11,
  input  in_12,
  input  I0,
  output O7,
  output out_15,
  output out_16,
  output out_17,
  output out_18,
  output out_19,
  output out_20,
  output O0
);

  wire and_1_out, and_2_out, and_3_out, and_4_out, and_5_out, and_6_out, and_7_out, and_8_out, and_9_out,
       and_10_out, and_11_out, and_12_out, and_13_out, and_14_out, and_15_out, and_16_out, j_k_ff_1_q,
       j_k_ff_2_q, j_k_ff_2_qn, j_k_ff_3_q, j_k_ff_3_qn, j_k_ff_4_q, j_k_ff_4_qn, j_k_ff_5_q, j_k_ff_5_qn,
       j_k_ff_6_q, j_k_ff_6_qn, j_k_ff_7_q, j_k_ff_7_qn, j_k_ff_8_q, j_k_ff_8_qn, or_1_out, or_2_out,
       or_3_out, or_4_out, or_5_out, or_6_out, or_7_out, or_8_out;

  assign O7 = COut ? j_k_ff_1_q : 1'bz;  // Controlled_Buffer controlled_buffer_1
  J_K_Flip_Flop j_k_ff_1 (
    .J(CEnable), .K(CEnable), .clk(j_k_ff_2_qn), .Q(j_k_ff_1_q), .preset(and_1_out), .reset(or_1_out));  // open: Qn
  or or_1 (or_1_out, CReset, and_2_out);
  and and_1 (and_1_out, CWrite, I7, Clock);
  and and_2 (and_2_out, CWrite, ~I7, Clock);  // AND_Gate
  J_K_Flip_Flop j_k_ff_2 (
    .J(CEnable), .K(CEnable), .clk(j_k_ff_3_qn), .Q(j_k_ff_2_q), .Qn(j_k_ff_2_qn), .preset(and_3_out),
    .reset(or_2_out));
  or or_2 (or_2_out, CReset, and_4_out);
  and and_3 (and_3_out, CWrite, in_7, Clock);
  and and_4 (and_4_out, CWrite, ~in_7, Clock);  // AND_Gate
  assign out_15 = COut ? j_k_ff_2_q : 1'bz;  // Controlled_Buffer controlled_buffer_2
  J_K_Flip_Flop j_k_ff_3 (
    .J(CEnable), .K(CEnable), .clk(j_k_ff_4_qn), .Q(j_k_ff_3_q), .Qn(j_k_ff_3_qn), .preset(and_5_out),
    .reset(or_3_out));
  or or_3 (or_3_out, CReset, and_6_out);
  and and_5 (and_5_out, CWrite, in_8, Clock);
  assign out_16 = COut ? j_k_ff_3_q : 1'bz;  // Controlled_Buffer controlled_buffer_3
  J_K_Flip_Flop j_k_ff_4 (
    .J(CEnable), .K(CEnable), .clk(j_k_ff_5_qn), .Q(j_k_ff_4_q), .Qn(j_k_ff_4_qn), .preset(and_7_out),
    .reset(or_4_out));
  and and_6 (and_6_out, CWrite, ~in_8, Clock);  // AND_Gate
  and and_7 (and_7_out, CWrite, in_9, Clock);
  assign out_17 = COut ? j_k_ff_4_q : 1'bz;  // Controlled_Buffer controlled_buffer_4
  or or_4 (or_4_out, CReset, and_8_out);
  and and_8 (and_8_out, CWrite, ~in_9, Clock);  // AND_Gate
  assign out_18 = COut ? j_k_ff_5_q : 1'bz;  // Controlled_Buffer controlled_buffer_5
  J_K_Flip_Flop j_k_ff_5 (
    .J(CEnable), .K(CEnable), .clk(j_k_ff_6_qn), .Q(j_k_ff_5_q), .Qn(j_k_ff_5_qn), .preset(and_9_out),
    .reset(or_5_out));
  or or_5 (or_5_out, CReset, and_10_out);
  and and_9 (and_9_out, CWrite, in_10, Clock);
  and and_10 (and_10_out, CWrite, ~in_10, Clock);  // AND_Gate
  J_K_Flip_Flop j_k_ff_6 (
    .J(CEnable), .K(CEnable), .clk(j_k_ff_7_qn), .Q(j_k_ff_6_q), .Qn(j_k_ff_6_qn), .preset(and_11_out),
    .reset(or_6_out));
  or or_6 (or_6_out, CReset, and_12_out);
  and and_11 (and_11_out, CWrite, in_11, Clock);
  and and_12 (and_12_out, CWrite, ~in_11, Clock);  // AND_Gate
  assign out_19 = COut ? j_k_ff_6_q : 1'bz;  // Controlled_Buffer controlled_buffer_6
  J_K_Flip_Flop j_k_ff_7 (
    .J(CEnable), .K(CEnable), .clk(j_k_ff_8_qn), .Q(j_k_ff_7_q), .Qn(j_k_ff_7_qn), .preset(and_13_out),
    .reset(or_7_out));
  or or_7 (or_7_out, CReset, and_15_out);
  and and_13 (and_13_out, CWrite, in_12, Clock);
  assign out_20 = COut ? j_k_ff_7_q : 1'bz;  // Controlled_Buffer controlled_buffer_7
  J_K_Flip_Flop j_k_ff_8 (
    .J(CEnable), .K(CEnable), .clk(Clock), .Q(j_k_ff_8_q), .Qn(j_k_ff_8_qn), .preset(and_14_out),
    .reset(or_8_out));
  and and_14 (and_14_out, CWrite, I0, Clock);
  and and_15 (and_15_out, CWrite, ~in_12, Clock);  // AND_Gate
  assign O0 = COut ? j_k_ff_8_q : 1'bz;  // Controlled_Buffer controlled_buffer_8
  or or_8 (or_8_out, CReset, and_16_out);
  and and_16 (and_16_out, CWrite, ~I0, Clock);  // AND_Gate
endmodule

module memory_new_small (
  input  clock,
  input  read,
  input  write,
  input  D7,
  input  in_5,
  input  in_6,
  input  in_7,
  input  in_8,
  input  in_9,
  input  in_10,
  input  D0,
  input  A3,
  input  in_13,
  input  in_14,
  input  A0,
  output Q7,
  output out_17,
  output out_18,
  output out_19,
  output out_20,
  output out_21,
  output out_22,
  output Q0
);

  wire and_1_out, and_2_out, and_3_out, and_4_out, and_5_out, and_6_out, and_7_out, and_8_out, and_9_out,
       and_10_out, and_11_out, and_12_out, and_13_out, and_14_out, and_15_out, and_16_out, and_17_out,
       and_18_out, and_19_out, and_20_out, and_21_out, and_22_out, and_23_out, and_24_out, and_25_out,
       and_26_out, and_27_out, and_28_out, and_29_out, and_30_out, and_31_out, and_32_out, R, R_1, R_2, R_3,
       R_4, R_5, R_6, R_7, R_8, R_9, R_10, R_11, R_12, R_13, R_14, R_15;

  decoder decoder_1 (
    .D0(A0), .in_2(in_14), .in_3(in_13), .in_4(A3), .out_5(R_15), .out_6(R_14), .out_7(R_13), .out_8(R_12),
    .out_9(R_11), .out_10(R_10), .out_11(R_9), .out_12(R_8), .out_13(R_7), .out_14(R_6), .out_15(R_5),
    .out_16(R_4), .out_17(R_3), .out_18(R_2), .out_19(R_1), .out_20(R));
  register register_1 (
    .Q0(Q0), .Q1(out_22), .Q2(out_21), .Q3(out_20), .Q4(out_19), .Q5(out_18), .Q6(out_17), .Q7(Q7),
    .en_input(and_1_out), .clock(clock), .D0(D0), .D1(in_10), .D2(in_9), .D3(in_8), .D4(in_7), .D5(in_6),
    .D6(in_5), .D7(D7), .en_output(and_2_out));  // open: out_12, out_13, out_14, out_15, out_16, out_17, out_18, DG0
  register register_2 (
    .Q0(Q0), .Q1(out_22), .Q2(out_21), .Q3(out_20), .Q4(out_19), .Q5(out_18), .Q6(out_17), .Q7(Q7),
    .en_input(and_3_out), .clock(clock), .D0(D0), .D1(in_10), .D2(in_9), .D3(in_8), .D4(in_7), .D5(in_6),
    .D6(in_5), .D7(D7), .en_output(and_4_out));  // open: out_12, out_13, out_14, out_15, out_16, out_17, out_18, DG0
  register register_3 (
    .Q0(Q0), .Q1(out_22), .Q2(out_21), .Q3(out_20), .Q4(out_19), .Q5(out_18), .Q6(out_17), .Q7(Q7),
    .en_input(and_5_out), .clock(clock), .D0(D0), .D1(in_10), .D2(in_9), .D3(in_8), .D4(in_7), .D5(in_6),
    .D6(in_5), .D7(D7), .en_output(and_6_out));  // open: out_12, out_13, out_14, out_15, out_16, out_17, out_18, DG0
  register register_4 (
    .Q0(Q0), .Q1(out_22), .Q2(out_21), .Q3(out_20), .Q4(out_19), .Q5(out_18), .Q6(out_17), .Q7(Q7),
    .en_input(and_7_out), .clock(clock), .D0(D0), .D1(in_10), .D2(in_9), .D3(in_8), .D4(in_7), .D5(in_6),
    .D6(in_5), .D7(D7), .en_output(and_8_out));  // open: out_12, out_13, out_14, out_15, out_16, out_17, out_18, DG0
  and and_1 (and_1_out, write, R);
  and and_2 (and_2_out, R, read);
  and and_3 (and_3_out, write, R_4);
  and and_4 (and_4_out, R_4, read);
  and and_5 (and_5_out, write, R_8);
  and and_6 (and_6_out, R_8, read);
  and and_7 (and_7_out, write, R_12);
  and and_8 (and_8_out, R_12, read);
  and and_9 (and_9_out, write, R_1);
  and and_10 (and_10_out, R_1, read);
  register register_5 (
    .Q0(Q0), .Q1(out_22), .Q2(out_21), .Q3(out_20), .Q4(out_19), .Q5(out_18), .Q6(out_17), .Q7(Q7),
    .en_input(and_9_out), .clock(clock), .D0(D0), .D1(in_10), .D2(in_9), .D3(in_8), .D4(in_7), .D5(in_6),
    .D6(in_5), .D7(D7), .en_output(and_10_out));  // open: out_12, out_13, out_14, out_15, out_16, out_17, out_18, DG0
  and and_11 (and_11_out, write, R_5);
  and and_12 (and_12_out, R_5, read);
  register register_6 (
    .Q0(Q0), .Q1(out_22), .Q2(out_21), .Q3(out_20), .Q4(out_19), .Q5(out_18), .Q6(out_17), .Q7(Q7),
    .en_input(and_11_out), .clock(clock), .D0(D0), .D1(in_10), .D2(in_9), .D3(in_8), .D4(in_7), .D5(in_6),
    .D6(in_5), .D7(D7), .en_output(and_12_out));  // open: out_12, out_13, out_14, out_15, out_16, out_17, out_18, DG0
  and and_13 (and_13_out, write, R_9);
  and and_14 (and_14_out, R_9, read);
  register register_7 (
    .Q0(Q0), .Q1(out_22), .Q2(out_21), .Q3(out_20), .Q4(out_19), .Q5(out_18), .Q6(out_17), .Q7(Q7),
    .en_input(and_13_out), .clock(clock), .D0(D0), .D1(in_10), .D2(in_9), .D3(in_8), .D4(in_7), .D5(in_6),
    .D6(in_5), .D7(D7), .en_output(and_14_out));  // open: out_12, out_13, out_14, out_15, out_16, out_17, out_18, DG0
  and and_15 (and_15_out, write, R_13);
  and and_16 (and_16_out, R_13, read);
  register register_8 (
    .Q0(Q0), .Q1(out_22), .Q2(out_21), .Q3(out_20), .Q4(out_19), .Q5(out_18), .Q6(out_17), .Q7(Q7),
    .en_input(and_15_out), .clock(clock), .D0(D0), .D1(in_10), .D2(in_9), .D3(in_8), .D4(in_7), .D5(in_6),
    .D6(in_5), .D7(D7), .en_output(and_16_out));  // open: out_12, out_13, out_14, out_15, out_16, out_17, out_18, DG0
  register register_9 (
    .Q0(Q0), .Q1(out_22), .Q2(out_21), .Q3(out_20), .Q4(out_19), .Q5(out_18), .Q6(out_17), .Q7(Q7),
    .en_input(and_17_out), .clock(clock), .D0(D0), .D1(in_10), .D2(in_9), .D3(in_8), .D4(in_7), .D5(in_6),
    .D6(in_5), .D7(D7), .en_output(and_18_out));  // open: out_12, out_13, out_14, out_15, out_16, out_17, out_18, DG0
  register register_10 (
    .Q0(Q0), .Q1(out_22), .Q2(out_21), .Q3(out_20), .Q4(out_19), .Q5(out_18), .Q6(out_17), .Q7(Q7),
    .en_input(and_19_out), .clock(clock), .D0(D0), .D1(in_10), .D2(in_9), .D3(in_8), .D4(in_7), .D5(in_6),
    .D6(in_5), .D7(D7), .en_output(and_20_out));  // open: out_12, out_13, out_14, out_15, out_16, out_17, out_18, DG0
  register register_11 (
    .Q0(Q0), .Q1(out_22), .Q2(out_21), .Q3(out_20), .Q4(out_19), .Q5(out_18), .Q6(out_17), .Q7(Q7),
    .en_input(and_21_out), .clock(clock), .D0(D0), .D1(in_10), .D2(in_9), .D3(in_8), .D4(in_7), .D5(in_6),
    .D6(in_5), .D7(D7), .en_output(and_22_out));  // open: out_12, out_13, out_14, out_15, out_16, out_17, out_18, DG0
  register register_12 (
    .Q0(Q0), .Q1(out_22), .Q2(out_21), .Q3(out_20), .Q4(out_19), .Q5(out_18), .Q6(out_17), .Q7(Q7),
    .en_input(and_23_out), .clock(clock), .D0(D0), .D1(in_10), .D2(in_9), .D3(in_8), .D4(in_7), .D5(in_6),
    .D6(in_5), .D7(D7), .en_output(and_24_out));  // open: out_12, out_13, out_14, out_15, out_16, out_17, out_18, DG0
  and and_17 (and_17_out, write, R_2);
  and and_18 (and_18_out, R_2, read);
  and and_19 (and_19_out, write, R_6);
  and and_20 (and_20_out, R_6, read);
  and and_21 (and_21_out, write, R_10);
  and and_22 (and_22_out, R_10, read);
  and and_23 (and_23_out, write, R_14);
  and and_24 (and_24_out, R_14, read);
  and and_25 (and_25_out, write, R_3);
  and and_26 (and_26_out, R_3, read);
  register register_13 (
    .Q0(Q0), .Q1(out_22), .Q2(out_21), .Q3(out_20), .Q4(out_19), .Q5(out_18), .Q6(out_17), .Q7(Q7),
    .en_input(and_25_out), .clock(clock), .D0(D0), .D1(in_10), .D2(in_9), .D3(in_8), .D4(in_7), .D5(in_6),
    .D6(in_5), .D7(D7), .en_output(and_26_out));  // open: out_12, out_13, out_14, out_15, out_16, out_17, out_18, DG0
  and and_27 (and_27_out, write, R_7);
  and and_28 (and_28_out, R_7, read);
  register register_14 (
    .Q0(Q0), .Q1(out_22), .Q2(out_21), .Q3(out_20), .Q4(out_19), .Q5(out_18), .Q6(out_17), .Q7(Q7),
    .en_input(and_27_out), .clock(clock), .D0(D0), .D1(in_10), .D2(in_9), .D3(in_8), .D4(in_7), .D5(in_6),
    .D6(in_5), .D7(D7), .en_output(and_28_out));  // open: out_12, out_13, out_14, out_15, out_16, out_17, out_18, DG0
  and and_29 (and_29_out, write, R_11);
  and and_30 (and_30_out, R_11, read);
  register register_15 (
    .Q0(Q0), .Q1(out_22), .Q2(out_21), .Q3(out_20), .Q4(out_19), .Q5(out_18), .Q6(out_17), .Q7(Q7),
    .en_input(and_29_out), .clock(clock), .D0(D0), .D1(in_10), .D2(in_9), .D3(in_8), .D4(in_7), .D5(in_6),
    .D6(in_5), .D7(D7), .en_output(and_30_out));  // open: out_12, out_13, out_14, out_15, out_16, out_17, out_18, DG0
  and and_31 (and_31_out, write, R_15);
  and and_32 (and_32_out, R_15, read);
  register register_16 (
    .Q0(Q0), .Q1(out_22), .Q2(out_21), .Q3(out_20), .Q4(out_19), .Q5(out_18), .Q6(out_17), .Q7(Q7),
    .en_input(and_31_out), .clock(clock), .D0(D0), .D1(in_10), .D2(in_9), .D3(in_8), .D4(in_7), .D5(in_6),
    .D6(in_5), .D7(D7), .en_output(and_32_out));  // open: out_12, out_13, out_14, out_15, out_16, out_17, out_18, DG0

  // Other names for the same wires on the sheet: D[6:1] = {in_5, in_6, in_7, in_8, in_9, in_10};
  //   Q[6:1] = {out_17, out_18, out_19, out_20, out_21, out_22}
endmodule

module mem_new_big (
  input  clock,
  input  read,
  input  write,
  input  D7,
  input  in_5,
  input  in_6,
  input  in_7,
  input  in_8,
  input  in_9,
  input  in_10,
  input  D0,
  input  A3,
  input  in_13,
  input  in_14,
  input  A0,
  input  A7,
  input  in_17,
  input  in_18,
  input  A5,
  output Q7,
  output out_21,
  output out_22,
  output out_23,
  output out_24,
  output out_25,
  output out_26,
  output Q0
);

  wire and_1_out, and_2_out, and_3_out, and_4_out, and_5_out, and_6_out, and_7_out, and_8_out, and_9_out,
       and_10_out, and_11_out, and_12_out, and_13_out, and_14_out, and_15_out, and_16_out, and_17_out,
       and_18_out, and_19_out, and_20_out, and_21_out, and_22_out, and_23_out, and_24_out, and_25_out,
       and_26_out, and_27_out, and_28_out, and_29_out, and_30_out, and_31_out, and_32_out,
       memory_new_small_1_p1, memory_new_small_2_p1, memory_new_small_3_p1, memory_new_small_4_p1, R, R_1,
       R_2, R_3, R_4, R_5, R_6, R_7, R_8, R_9, R_10, R_11, R_12, R_13, R_14, R_15;

  decoder decoder_1 (
    .D0(A5), .in_2(in_18), .in_3(in_17), .in_4(A7), .out_5(R_15), .out_6(R_14), .out_7(R_13), .out_8(R_12),
    .out_9(R_11), .out_10(R_10), .out_11(R_9), .out_12(R_8), .out_13(R_7), .out_14(R_6), .out_15(R_5),
    .out_16(R_4), .out_17(R_3), .out_18(R_2), .out_19(R_1), .out_20(R));
  // memory_new_small memory_new_small_1: pin names not known; wires that end beside it: memory_new_small_1_p1, memory_new_small_1_p1, D0, in_10, in_9, in_8, in_7, in_6, in_5
  // memory_new_small memory_new_small_2: pin names not known; wires that end beside it: memory_new_small_2_p1, memory_new_small_2_p1, D0, in_10, in_9, in_8, in_7, in_6, in_5
  // memory_new_small memory_new_small_3: pin names not known; wires that end beside it: memory_new_small_3_p1, memory_new_small_3_p1, D0, in_10, in_9, in_8, in_7, in_6, in_5
  // memory_new_small memory_new_small_4: pin names not known; wires that end beside it: memory_new_small_4_p1, memory_new_small_4_p1, D0, in_10, in_9, in_8, in_7, in_6, in_5
  and and_1 (and_1_out, write, R);
  and and_2 (and_2_out, R, read);
  and and_3 (and_3_out, write, R_4);
  and and_4 (and_4_out, R_4, read);
  and and_5 (and_5_out, write, R_8);
  and and_6 (and_6_out, R_8, read);
  and and_7 (and_7_out, write, R_12);
  and and_8 (and_8_out, R_12, read);
  // memory_new_small memory_new_small_5: pin names not known; wires that end beside it: write, R, read, D0, in_10, in_9, in_8, in_7, in_6, in_5
  // memory_new_small memory_new_small_6: pin names not known; wires that end beside it: write, R_4, read, D0, in_10, in_9, in_8, in_7, in_6, in_5
  // memory_new_small memory_new_small_7: pin names not known; wires that end beside it: write, R_8, read, D0, in_10, in_9, in_8, in_7, in_6, in_5
  // memory_new_small memory_new_small_8: pin names not known; wires that end beside it: write, R_12, read, D0, in_10, in_9, in_8, in_7, in_6, in_5
  and and_9 (and_9_out, write, R_1);
  and and_10 (and_10_out, R_1, read);
  and and_11 (and_11_out, write, R_5);
  and and_12 (and_12_out, R_5, read);
  and and_13 (and_13_out, write, R_9);
  and and_14 (and_14_out, R_9, read);
  and and_15 (and_15_out, write, R_13);
  and and_16 (and_16_out, R_13, read);
  // memory_new_small memory_new_small_9: pin names not known; wires that end beside it: write, R_1, read, D0, in_10, in_9, in_8, in_7, in_6, in_5
  // memory_new_small memory_new_small_10: pin names not known; wires that end beside it: write, R_5, read, D0, in_10, in_9, in_8, in_7, in_6, in_5
  // memory_new_small memory_new_small_11: pin names not known; wires that end beside it: write, R_9, read, D0, in_10, in_9, in_8, in_7, in_6, in_5
  // memory_new_small memory_new_small_12: pin names not known; wires that end beside it: write, R_13, read, D0, in_10, in_9, in_8, in_7, in_6, in_5
  and and_17 (and_17_out, write, R_2);
  and and_18 (and_18_out, R_2, read);
  and and_19 (and_19_out, write, R_6);
  and and_20 (and_20_out, R_6, read);
  and and_21 (and_21_out, write, R_10);
  and and_22 (and_22_out, R_10, read);
  and and_23 (and_23_out, write, R_14);
  and and_24 (and_24_out, R_14, read);
  // memory_new_small memory_new_small_13: pin names not known; wires that end beside it: write, R_2, read, D0, in_10, in_9, in_8, in_7, in_6, in_5
  // memory_new_small memory_new_small_14: pin names not known; wires that end beside it: write, R_6, read, D0, in_10, in_9, in_8, in_7, in_6, in_5
  // memory_new_small memory_new_small_15: pin names not known; wires that end beside it: write, R_10, read, D0, in_10, in_9, in_8, in_7, in_6, in_5
  // memory_new_small memory_new_small_16: pin names not known; wires that end beside it: write, R_14, read, D0, in_10, in_9, in_8, in_7, in_6, in_5
  and and_25 (and_25_out, write, R_3);
  and and_26 (and_26_out, R_3, read);
  and and_27 (and_27_out, write, R_7);
  and and_28 (and_28_out, R_7, read);
  and and_29 (and_29_out, write, R_11);
  and and_30 (and_30_out, R_11, read);
  and and_31 (and_31_out, write, R_15);
  and and_32 (and_32_out, R_15, read);

  // Other names for the same wires on the sheet: addr[3:0] = {A3, in_13, in_14, A0};
  //   D[6:1] = {in_5, in_6, in_7, in_8, in_9, in_10}; Q[6:1] = {out_21, out_22, out_23, out_24, out_25, out_26}
endmodule

module program_loader (
  input  [7:0] DATA,
  input  en,
  output [7:0] ADDR
);

  Counter_8_bits counter_8_bits_1 (
    .COut(en), .CEnable(en), .O7(ADDR[0]), .out_15(ADDR[1]), .out_16(ADDR[2]), .out_17(ADDR[3]),
    .out_18(ADDR[4]), .out_19(ADDR[5]), .out_20(ADDR[6]), .O0(ADDR[7]));  // open: CWrite, CReset, Clock, I7, in_7, in_8, in_9, in_10, in_11, in_12, I0
endmodule

module alu (
  input  [7:0] X,
  input  [7:0] Y,
  input  CARRY_IN,
  input  [7:0] A,
  input  CLOCK,
  input  ALU_EN,
  input  ALU_CTRL0,
  input  ALU_CTRL1,
  input  ALU_CTRL2,
  output CARRY_OUT
);

  wire B_OR_SUB0, B_OR_SUB1, B_OR_SUB2, B_OR_SUB3, B_OR_SUB4, B_OR_SUB5, B_OR_SUB6, B_OR_SUB7,
       bus_transceiver_1_out_10, bus_transceiver_1_out_11, bus_transceiver_1_out_12,
       bus_transceiver_1_out_13, bus_transceiver_1_out_14, bus_transceiver_1_out_15,
       bus_transceiver_1_out_16, bus_transceiver_1_out_17, CALC, Cin_OR_SUB, n7404_2_pin2, n7404_2_pin8,
       n7404_2_pin10, n7404_2_pin12, n7404_3_pin2, n7404_3_pin8, n7404_3_pin10, n7404_3_pin12, n7408_1_pin3,
       n7408_1_pin6, n7408_1_pin8, n7408_1_pin11, n7408_2_pin3, n7408_2_pin6, n7408_2_pin8, n7408_2_pin11,
       n7408_3_pin3, n7408_3_pin6, n7408_3_pin8, n7408_3_pin11, n7408_4_pin3, n7408_4_pin6, n7408_4_pin8,
       n7408_4_pin11, n7408_5_pin3, n7408_5_pin6, n7408_5_pin8, n7408_5_pin11, n7408_6_pin3, n7408_6_pin6,
       n7408_6_pin8, n7408_6_pin11, n7432_1_pin3, n7432_1_pin6, n7432_1_pin8, n7432_1_pin11, n7432_2_pin3,
       n7432_2_pin6, n7432_2_pin8, n7432_2_pin11, n7432_6_pin11, n7486_3_pin1, n7486_3_pin2, n7486_3_pin3,
       n7486_3_pin5, n7486_3_pin6, n7486_4_pin3, n7486_4_pin6, n7486_4_pin8, n7486_4_pin11, n7486_5_pin3,
       n7486_5_pin6, n7486_5_pin8, n7486_5_pin11, n7486_6_pin1, n7486_6_pin2, n7486_6_pin3, n7486_6_pin4,
       n7486_6_pin5, n7486_6_pin6, n7486_7_pin1, n7486_7_pin2, n7486_7_pin3, n7486_7_pin4, n7486_7_pin5,
       n7486_7_pin6, n7486_8_pin1, n7486_8_pin2, n7486_8_pin3, n7486_8_pin4, n7486_8_pin5, n7486_8_pin6,
       NotCtrl0, NotCtrl1, NotCtrl2, S_ADD, S_AND, S_NOT, S_OR, S_SUB, S_XOR, xor_2_out;

  _7404 u_7404_1 (
    .pin13(ALU_CTRL2), .pin12(NotCtrl2), .pin11(ALU_CTRL1), .pin10(NotCtrl1), .pin9(ALU_CTRL0),
    .pin8(NotCtrl0));  // open: pin1, pin2, pin3, pin4, pin5, pin6
  _7411 u_7411_1 (
    .pin1(NotCtrl1), .pin2(NotCtrl2), .pin3(NotCtrl0), .pin4(ALU_CTRL1), .pin5(NotCtrl2), .pin6(S_AND),
    .pin13(ALU_CTRL0), .pin12(S_SUB), .pin11(NotCtrl2), .pin10(NotCtrl1), .pin9(NotCtrl0), .pin8(S_ADD));
  _7411 u_7411_2 (
    .pin1(NotCtrl1), .pin2(ALU_CTRL2), .pin3(ALU_CTRL0), .pin4(NotCtrl1), .pin5(ALU_CTRL2), .pin6(S_NOT),
    .pin13(NotCtrl0), .pin12(S_XOR), .pin11(NotCtrl2), .pin10(ALU_CTRL1), .pin9(ALU_CTRL0), .pin8(S_OR));
  _7486 u_7486_1 (
    .pin1(S_SUB), .pin2(Y[3]), .pin3(B_OR_SUB3), .pin4(S_SUB), .pin5(Y[2]), .pin6(B_OR_SUB2), .pin13(S_SUB),
    .pin12(Y[1]), .pin11(B_OR_SUB1), .pin10(S_SUB), .pin9(Y[0]), .pin8(B_OR_SUB0));
  _7486 u_7486_2 (
    .pin1(S_SUB), .pin2(Y[7]), .pin3(B_OR_SUB7), .pin4(S_SUB), .pin5(Y[6]), .pin6(B_OR_SUB6), .pin13(S_SUB),
    .pin12(Y[5]), .pin11(B_OR_SUB5), .pin10(S_SUB), .pin9(Y[4]), .pin8(B_OR_SUB4));
  or or_1 (CALC, S_ADD, S_SUB);
  xor xor_1 (Cin_OR_SUB, S_SUB, CARRY_IN);
  _7486 u_7486_3 (
    .pin1(n7486_3_pin1), .pin2(n7486_3_pin2), .pin3(n7486_3_pin3), .pin4(Cin_OR_SUB), .pin5(n7486_3_pin5),
    .pin6(n7486_3_pin6), .pin13(B_OR_SUB1), .pin12(X[1]), .pin11(n7486_3_pin1), .pin10(B_OR_SUB0),
    .pin9(X[0]), .pin8(n7486_3_pin5));
  _7408 u_7408_1 (
    .pin1(X[2]), .pin2(Y[2]), .pin3(n7408_1_pin3), .pin4(X[3]), .pin5(Y[3]), .pin6(n7408_1_pin6),
    .pin13(Y[1]), .pin12(X[1]), .pin11(n7408_1_pin11), .pin10(Y[0]), .pin9(X[0]), .pin8(n7408_1_pin8));
  _7408 u_7408_2 (
    .pin1(X[6]), .pin2(Y[6]), .pin3(n7408_2_pin3), .pin4(X[7]), .pin5(Y[7]), .pin6(n7408_2_pin6),
    .pin13(Y[5]), .pin12(X[5]), .pin11(n7408_2_pin11), .pin10(Y[4]), .pin9(X[4]), .pin8(n7408_2_pin8));
  _7432 u_7432_1 (
    .pin1(X[3]), .pin2(Y[3]), .pin3(n7432_1_pin3), .pin4(X[2]), .pin5(Y[2]), .pin6(n7432_1_pin6),
    .pin13(Y[1]), .pin12(X[1]), .pin11(n7432_1_pin11), .pin10(Y[0]), .pin9(X[0]), .pin8(n7432_1_pin8));
  _7432 u_7432_2 (
    .pin1(X[7]), .pin2(Y[7]), .pin3(n7432_2_pin3), .pin4(X[6]), .pin5(Y[6]), .pin6(n7432_2_pin6),
    .pin13(Y[5]), .pin12(X[5]), .pin11(n7432_2_pin11), .pin10(Y[4]), .pin9(X[4]), .pin8(n7432_2_pin8));
  _7486 u_7486_4 (
    .pin1(X[3]), .pin2(Y[3]), .pin3(n7486_4_pin3), .pin4(X[2]), .pin5(Y[2]), .pin6(n7486_4_pin6),
    .pin13(Y[1]), .pin12(X[1]), .pin11(n7486_4_pin11), .pin10(Y[0]), .pin9(X[0]), .pin8(n7486_4_pin8));
  _7486 u_7486_5 (
    .pin1(X[7]), .pin2(Y[7]), .pin3(n7486_5_pin3), .pin4(X[6]), .pin5(Y[6]), .pin6(n7486_5_pin6),
    .pin13(Y[5]), .pin12(X[5]), .pin11(n7486_5_pin11), .pin10(Y[4]), .pin9(X[4]), .pin8(n7486_5_pin8));
  _7404 u_7404_2 (
    .pin1(X[3]), .pin2(n7404_2_pin2), .pin13(X[2]), .pin12(n7404_2_pin12), .pin11(X[1]),
    .pin10(n7404_2_pin10), .pin9(X[0]), .pin8(n7404_2_pin8));  // open: pin3, pin4, pin5, pin6
  _7404 u_7404_3 (
    .pin1(X[7]), .pin2(n7404_3_pin2), .pin13(X[6]), .pin12(n7404_3_pin12), .pin11(X[5]),
    .pin10(n7404_3_pin10), .pin9(X[4]), .pin8(n7404_3_pin8));  // open: pin3, pin4, pin5, pin6
  _7486 u_7486_6 (
    .pin1(n7486_6_pin1), .pin2(n7486_6_pin2), .pin3(n7486_6_pin3), .pin4(n7486_6_pin4), .pin5(n7486_6_pin5),
    .pin6(n7486_6_pin6), .pin13(B_OR_SUB3), .pin12(X[3]), .pin11(n7486_6_pin1), .pin10(B_OR_SUB2),
    .pin9(X[2]), .pin8(n7486_6_pin5));
  _7486 u_7486_7 (
    .pin1(n7486_7_pin1), .pin2(n7486_7_pin2), .pin3(n7486_7_pin3), .pin4(n7486_7_pin4), .pin5(n7486_7_pin5),
    .pin6(n7486_7_pin6), .pin13(B_OR_SUB5), .pin12(X[5]), .pin11(n7486_7_pin1), .pin10(B_OR_SUB4),
    .pin9(X[4]), .pin8(n7486_7_pin5));
  _7486 u_7486_8 (
    .pin1(n7486_8_pin1), .pin2(n7486_8_pin2), .pin3(n7486_8_pin3), .pin4(n7486_8_pin4), .pin5(n7486_8_pin5),
    .pin6(n7486_8_pin6), .pin13(B_OR_SUB7), .pin12(X[7]), .pin11(n7486_8_pin1), .pin10(B_OR_SUB6),
    .pin9(X[6]), .pin8(n7486_8_pin5));
  bus_transceiver bus_transceiver_1 (
    .in_1(n7408_1_pin8), .in_2(n7408_1_pin11), .in_3(n7408_1_pin3), .in_4(n7408_1_pin6), .in_5(n7408_2_pin8),
    .in_6(n7408_2_pin11), .in_7(n7408_2_pin3), .in_8(n7408_2_pin6), .enable(S_AND),
    .out_10(bus_transceiver_1_out_10), .out_11(bus_transceiver_1_out_11), .out_12(bus_transceiver_1_out_12),
    .out_13(bus_transceiver_1_out_13), .out_14(bus_transceiver_1_out_14), .out_15(bus_transceiver_1_out_15),
    .out_16(bus_transceiver_1_out_16), .out_17(bus_transceiver_1_out_17));
  bus_transceiver bus_transceiver_2 (
    .in_1(n7432_1_pin8), .in_2(n7432_1_pin11), .in_3(n7432_1_pin6), .in_4(n7432_1_pin3), .in_5(n7432_2_pin8),
    .in_6(n7432_2_pin11), .in_7(n7432_2_pin6), .in_8(n7432_2_pin3), .enable(S_OR),
    .out_10(bus_transceiver_1_out_10), .out_11(bus_transceiver_1_out_11), .out_12(bus_transceiver_1_out_12),
    .out_13(bus_transceiver_1_out_13), .out_14(bus_transceiver_1_out_14), .out_15(bus_transceiver_1_out_15),
    .out_16(bus_transceiver_1_out_16), .out_17(bus_transceiver_1_out_17));
  _7408 u_7408_3 (
    .pin1(n7486_3_pin1), .pin2(n7486_3_pin2), .pin3(n7408_3_pin3), .pin4(n7486_3_pin5), .pin5(Cin_OR_SUB),
    .pin6(n7408_3_pin6), .pin13(X[1]), .pin12(B_OR_SUB1), .pin11(n7408_3_pin11), .pin10(X[0]),
    .pin9(B_OR_SUB0), .pin8(n7408_3_pin8));
  _7408 u_7408_4 (
    .pin1(n7486_6_pin1), .pin2(n7486_6_pin2), .pin3(n7408_4_pin3), .pin4(n7486_6_pin5), .pin5(n7486_6_pin4),
    .pin6(n7408_4_pin6), .pin13(X[3]), .pin12(B_OR_SUB3), .pin11(n7408_4_pin11), .pin10(X[2]),
    .pin9(B_OR_SUB2), .pin8(n7408_4_pin8));
  _7408 u_7408_5 (
    .pin1(n7486_7_pin1), .pin2(n7486_7_pin2), .pin3(n7408_5_pin3), .pin4(n7486_7_pin5), .pin5(n7486_7_pin4),
    .pin6(n7408_5_pin6), .pin13(X[5]), .pin12(B_OR_SUB5), .pin11(n7408_5_pin11), .pin10(X[4]),
    .pin9(B_OR_SUB4), .pin8(n7408_5_pin8));
  _7408 u_7408_6 (
    .pin1(n7486_8_pin1), .pin2(n7486_8_pin2), .pin3(n7408_6_pin3), .pin4(n7486_8_pin5), .pin5(n7486_8_pin4),
    .pin6(n7408_6_pin6), .pin13(X[7]), .pin12(B_OR_SUB7), .pin11(n7408_6_pin11), .pin10(X[6]),
    .pin9(B_OR_SUB6), .pin8(n7408_6_pin8));
  _7432 u_7432_3 (
    .pin13(n7408_3_pin11), .pin12(n7408_3_pin3), .pin11(n7486_6_pin4), .pin10(n7408_3_pin6),
    .pin9(n7408_3_pin8), .pin8(n7486_3_pin2));  // open: pin1, pin2, pin3, pin4, pin5, pin6
  bus_transceiver bus_transceiver_3 (
    .in_1(n7486_4_pin8), .in_2(n7486_4_pin11), .in_3(n7486_4_pin6), .in_4(n7486_4_pin3), .in_5(n7486_5_pin8),
    .in_6(n7486_5_pin11), .in_7(n7486_5_pin6), .in_8(n7486_5_pin3), .enable(S_XOR),
    .out_10(bus_transceiver_1_out_10), .out_11(bus_transceiver_1_out_11), .out_12(bus_transceiver_1_out_12),
    .out_13(bus_transceiver_1_out_13), .out_14(bus_transceiver_1_out_14), .out_15(bus_transceiver_1_out_15),
    .out_16(bus_transceiver_1_out_16), .out_17(bus_transceiver_1_out_17));
  _7432 u_7432_4 (
    .pin13(n7408_4_pin11), .pin12(n7408_4_pin3), .pin11(n7486_7_pin4), .pin10(n7408_4_pin6),
    .pin9(n7408_4_pin8), .pin8(n7486_6_pin2));  // open: pin1, pin2, pin3, pin4, pin5, pin6
  _7432 u_7432_5 (
    .pin13(n7408_5_pin11), .pin12(n7408_5_pin3), .pin11(n7486_8_pin4), .pin10(n7408_5_pin6),
    .pin9(n7408_5_pin8), .pin8(n7486_7_pin2));  // open: pin1, pin2, pin3, pin4, pin5, pin6
  bus_transceiver bus_transceiver_4 (
    .in_1(n7404_2_pin8), .in_2(n7404_2_pin10), .in_3(n7404_2_pin12), .in_4(n7404_2_pin2),
    .in_5(n7404_3_pin8), .in_6(n7404_3_pin10), .in_7(n7404_3_pin12), .in_8(n7404_3_pin2), .enable(S_NOT),
    .out_10(bus_transceiver_1_out_10), .out_11(bus_transceiver_1_out_11), .out_12(bus_transceiver_1_out_12),
    .out_13(bus_transceiver_1_out_13), .out_14(bus_transceiver_1_out_14), .out_15(bus_transceiver_1_out_15),
    .out_16(bus_transceiver_1_out_16), .out_17(bus_transceiver_1_out_17));
  _7432 u_7432_6 (
    .pin13(n7408_6_pin11), .pin12(n7408_6_pin3), .pin11(n7432_6_pin11), .pin10(n7408_6_pin6),
    .pin9(n7408_6_pin8), .pin8(n7486_8_pin2));  // open: pin1, pin2, pin3, pin4, pin5, pin6
  bus_transceiver bus_transceiver_5 (
    .in_1(n7486_3_pin6), .in_2(n7486_3_pin3), .in_3(n7486_6_pin6), .in_4(n7486_6_pin3), .in_5(n7486_7_pin6),
    .in_6(n7486_7_pin3), .in_7(n7486_8_pin6), .in_8(n7486_8_pin3), .enable(CALC),
    .out_10(bus_transceiver_1_out_10), .out_11(bus_transceiver_1_out_11), .out_12(bus_transceiver_1_out_12),
    .out_13(bus_transceiver_1_out_13), .out_14(bus_transceiver_1_out_14), .out_15(bus_transceiver_1_out_15),
    .out_16(bus_transceiver_1_out_16), .out_17(bus_transceiver_1_out_17));
  xor xor_2 (xor_2_out, n7432_6_pin11, S_SUB);
  and and_1 (CARRY_OUT, xor_2_out, CALC);
  bus_transceiver bus_transceiver_6 (
    .in_1(bus_transceiver_1_out_10), .in_2(bus_transceiver_1_out_11), .in_3(bus_transceiver_1_out_12),
    .in_4(bus_transceiver_1_out_13), .in_5(bus_transceiver_1_out_14), .in_6(bus_transceiver_1_out_15),
    .in_7(bus_transceiver_1_out_16), .in_8(bus_transceiver_1_out_17), .enable(ALU_EN), .out_10(A[0]),
    .out_11(A[1]), .out_12(A[2]), .out_13(A[3]), .out_14(A[4]), .out_15(A[5]), .out_16(A[6]), .out_17(A[7]));

  // Other names for the same wires on the sheet: Ctrl0 = ALU_CTRL0; Ctrl1 = ALU_CTRL1; Ctrl2 = ALU_CTRL2; A1 = X[1];
  //   A2 = X[2]; A3 = X[3]; A4 = X[4]; A5 = X[5]; A6 = X[6]; A7 = X[7]; B0 = Y[0]; B1 = Y[1]; B2 = Y[2]; B3 = Y[3];
  //   B4 = Y[4]; B5 = Y[5]; B6 = Y[6]; B7 = Y[7]
endmodule
